// Logisim project FixedPointALU.circ as structural Verilog: 17 circuits, main circuit ALU_Test
module ALU_Test (
  input  C0,
  input  C1,
  input  C2,
  input  A0,
  input  A1,
  input  A2,
  input  A3,
  input  A4,
  input  A5,
  input  A6,
  input  A7,
  input  B0,
  input  B1,
  input  B2,
  input  B3,
  input  B4,
  input  B5,
  input  B6,
  input  B7,
  output Y0,
  output Y1,
  output Y2,
  output Y3,
  output Y4,
  output Y5,
  output Y6,
  output Y7,
  output OVERFLOW
);

  ALU alu_1 (
    .A3(A3), .A4(A4), .A5(A5), .A6(A6), .A7(A7), .B0(B0), .B1(B1), .B2(B2), .B3(B3), .B4(B4), .B5(B5),
    .B6(B6), .B7(B7), .C0(C0), .C1(C1), .C2(C2), .A0(A0), .A1(A1), .A2(A2), .Y0(Y0), .Y1(Y1), .Y2(Y2),
    .Y3(Y3), .Y4(Y4), .Y5(Y5), .Y6(Y6), .Y7(Y7), .OVERFLOW(OVERFLOW));

  // Notes on the sheet:
  //   INPUTS
  //   AND = 000
  //   OR = 010
  //   XOR = 100
  //   NOT = 110
  //   ADD = 001
  //   SUB = 011
  //   MUL = 101
  //   DIV = 111
  //   OUTPUTS
endmodule

module ALU (
  input  A0,
  input  A1,
  input  A2,
  input  A3,
  input  A4,
  input  A5,
  input  A6,
  input  A7,
  input  B0,
  input  B1,
  input  B2,
  input  B3,
  input  B4,
  input  B5,
  input  B6,
  input  B7,
  input  C0,
  input  C1,
  input  C2,
  output Y0,
  output Y1,
  output Y2,
  output Y3,
  output Y4,
  output Y5,
  output Y6,
  output Y7,
  output OVERFLOW
);

  wire alu_arithmetic_1_overflow, alu_arithmetic_1_y0, alu_arithmetic_1_y1, alu_arithmetic_1_y2,
       alu_arithmetic_1_y3, alu_arithmetic_1_y4, alu_arithmetic_1_y5, alu_arithmetic_1_y6,
       alu_arithmetic_1_y7, alu_logic_1_y0, alu_logic_1_y1, alu_logic_1_y2, alu_logic_1_y3, alu_logic_1_y4,
       alu_logic_1_y5, alu_logic_1_y6, alu_logic_1_y7;

  ALU_Logic alu_logic_1 (
    .A0(A0), .A1(A1), .A2(A2), .A3(A3), .A4(A4), .A5(A5), .A6(A6), .A7(A7), .B0(B0), .B1(B1), .B2(B2),
    .B3(B3), .B4(B4), .B5(B5), .B6(B6), .B7(B7), .C0(C0), .C1(C1), .Y0(alu_logic_1_y0), .Y1(alu_logic_1_y1),
    .Y2(alu_logic_1_y2), .Y3(alu_logic_1_y3), .Y4(alu_logic_1_y4), .Y5(alu_logic_1_y5), .Y6(alu_logic_1_y6),
    .Y7(alu_logic_1_y7));
  ALU_Arithmetic alu_arithmetic_1 (
    .A0(A0), .A1(A1), .A2(A2), .A3(A3), .A4(A4), .A5(A5), .A6(A6), .A7(A7), .B0(B0), .B1(B1), .B2(B2),
    .B3(B3), .B4(B4), .B5(B5), .B6(B6), .B7(B7), .C0(C0), .C1(C1), .Y0(alu_arithmetic_1_y0),
    .Y1(alu_arithmetic_1_y1), .Y2(alu_arithmetic_1_y2), .Y3(alu_arithmetic_1_y3), .Y4(alu_arithmetic_1_y4),
    .Y5(alu_arithmetic_1_y5), .Y6(alu_arithmetic_1_y6), .Y7(alu_arithmetic_1_y7),
    .OVERFLOW(alu_arithmetic_1_overflow));
  and and_1 (OVERFLOW, C2, alu_arithmetic_1_overflow);
  Multiplexer_x2 multiplexer_x2_1 (.C(C2), .D0(alu_logic_1_y0), .D1(alu_arithmetic_1_y0), .Y(Y0));
  Multiplexer_x2 multiplexer_x2_2 (.C(C2), .D0(alu_logic_1_y1), .D1(alu_arithmetic_1_y1), .Y(Y1));
  Multiplexer_x2 multiplexer_x2_3 (.C(C2), .D0(alu_logic_1_y2), .D1(alu_arithmetic_1_y2), .Y(Y2));
  Multiplexer_x2 multiplexer_x2_4 (.C(C2), .D0(alu_logic_1_y3), .D1(alu_arithmetic_1_y3), .Y(Y3));
  Multiplexer_x2 multiplexer_x2_5 (.C(C2), .D0(alu_logic_1_y4), .D1(alu_arithmetic_1_y4), .Y(Y4));
  Multiplexer_x2 multiplexer_x2_6 (.C(C2), .D0(alu_logic_1_y5), .D1(alu_arithmetic_1_y5), .Y(Y5));
  Multiplexer_x2 multiplexer_x2_7 (.C(C2), .D0(alu_logic_1_y6), .D1(alu_arithmetic_1_y6), .Y(Y6));
  Multiplexer_x2 multiplexer_x2_8 (.C(C2), .D0(alu_logic_1_y7), .D1(alu_arithmetic_1_y7), .Y(Y7));
endmodule

module ALU_Logic (
  input  A0,
  input  A1,
  input  A2,
  input  A3,
  input  A4,
  input  A5,
  input  A6,
  input  A7,
  input  B0,
  input  B1,
  input  B2,
  input  B3,
  input  B4,
  input  B5,
  input  B6,
  input  B7,
  input  C0,
  input  C1,
  output Y0,
  output Y1,
  output Y2,
  output Y3,
  output Y4,
  output Y5,
  output Y6,
  output Y7
);

  wire logic_and_1_y0, logic_and_1_y1, logic_and_1_y2, logic_and_1_y3, logic_and_1_y4, logic_and_1_y5,
       logic_and_1_y6, logic_and_1_y7, logic_or_1_y0, logic_or_1_y1, logic_or_1_y2, logic_or_1_y3,
       logic_or_1_y4, logic_or_1_y5, logic_or_1_y6, logic_or_1_y7, logic_xor_1_y0, logic_xor_1_y1,
       logic_xor_1_y2, logic_xor_1_y3, logic_xor_1_y4, logic_xor_1_y5, logic_xor_1_y6, logic_xor_1_y7,
       not_1_out, not_2_out, not_3_out, not_4_out, not_5_out, not_6_out, not_7_out, not_8_out;

  not not_1 (not_1_out, A0);
  not not_2 (not_2_out, A1);
  not not_3 (not_3_out, A2);
  not not_4 (not_4_out, A3);
  not not_5 (not_5_out, A4);
  not not_6 (not_6_out, A5);
  not not_7 (not_7_out, A6);
  not not_8 (not_8_out, A7);
  LOGIC_And logic_and_1 (
    .A0(A0), .B0(B0), .A1(A1), .B1(B1), .A2(A2), .B2(B2), .A3(A3), .B3(B3), .A4(A4), .B4(B4), .A5(A5),
    .B5(B5), .A6(A6), .B6(B6), .A7(A7), .B7(B7), .Y0(logic_and_1_y0), .Y1(logic_and_1_y1),
    .Y2(logic_and_1_y2), .Y3(logic_and_1_y3), .Y4(logic_and_1_y4), .Y5(logic_and_1_y5), .Y6(logic_and_1_y6),
    .Y7(logic_and_1_y7));
  LOGIC_Or logic_or_1 (
    .A0(A0), .B0(B0), .A1(A1), .B1(B1), .A2(A2), .B2(B2), .A3(A3), .B3(B3), .A4(A4), .B4(B4), .A5(A5),
    .B5(B5), .A6(A6), .B6(B6), .A7(A7), .B7(B7), .Y0(logic_or_1_y0), .Y1(logic_or_1_y1), .Y2(logic_or_1_y2),
    .Y3(logic_or_1_y3), .Y4(logic_or_1_y4), .Y5(logic_or_1_y5), .Y6(logic_or_1_y6), .Y7(logic_or_1_y7));
  LOGIC_Xor logic_xor_1 (
    .A0(A0), .B0(B0), .A1(A1), .B1(B1), .A2(A2), .B2(B2), .A3(A3), .B3(B3), .A4(A4), .B4(B4), .A5(A5),
    .B5(B5), .A6(A6), .B6(B6), .A7(A7), .B7(B7), .Y0(logic_xor_1_y0), .Y1(logic_xor_1_y1),
    .Y2(logic_xor_1_y2), .Y3(logic_xor_1_y3), .Y4(logic_xor_1_y4), .Y5(logic_xor_1_y5), .Y6(logic_xor_1_y6),
    .Y7(logic_xor_1_y7));
  Multiplexer_x4 multiplexer_x4_1 (
    .C0(C0), .C1(C1), .D0(logic_and_1_y0), .D1(logic_or_1_y0), .D2(logic_xor_1_y0), .D3(not_1_out), .Y(Y0));
  Multiplexer_x4 multiplexer_x4_2 (
    .C0(C0), .C1(C1), .D0(logic_and_1_y1), .D1(logic_or_1_y1), .D2(logic_xor_1_y1), .D3(not_2_out), .Y(Y1));
  Multiplexer_x4 multiplexer_x4_3 (
    .C0(C0), .C1(C1), .D0(logic_and_1_y2), .D1(logic_or_1_y2), .D2(logic_xor_1_y2), .D3(not_3_out), .Y(Y2));
  Multiplexer_x4 multiplexer_x4_4 (
    .C0(C0), .C1(C1), .D0(logic_and_1_y3), .D1(logic_or_1_y3), .D2(logic_xor_1_y3), .D3(not_4_out), .Y(Y3));
  Multiplexer_x4 multiplexer_x4_5 (
    .C0(C0), .C1(C1), .D0(logic_and_1_y4), .D1(logic_or_1_y4), .D2(logic_xor_1_y4), .D3(not_5_out), .Y(Y4));
  Multiplexer_x4 multiplexer_x4_6 (
    .C0(C0), .C1(C1), .D0(logic_and_1_y5), .D1(logic_or_1_y5), .D2(logic_xor_1_y5), .D3(not_6_out), .Y(Y5));
  Multiplexer_x4 multiplexer_x4_7 (
    .C0(C0), .C1(C1), .D0(logic_and_1_y6), .D1(logic_or_1_y6), .D2(logic_xor_1_y6), .D3(not_7_out), .Y(Y6));
  Multiplexer_x4 multiplexer_x4_8 (
    .C0(C0), .C1(C1), .D0(logic_and_1_y7), .D1(logic_or_1_y7), .D2(logic_xor_1_y7), .D3(not_8_out), .Y(Y7));
endmodule

module LOGIC_And (
  input  A0,
  input  B0,
  input  A1,
  input  B1,
  input  A2,
  input  B2,
  input  A3,
  input  B3,
  input  A4,
  input  B4,
  input  A5,
  input  B5,
  input  A6,
  input  B6,
  input  A7,
  input  B7,
  output Y0,
  output Y1,
  output Y2,
  output Y3,
  output Y4,
  output Y5,
  output Y6,
  output Y7
);

  and and_1 (Y0, A0, B0);
  and and_2 (Y1, A1, B1);
  and and_3 (Y2, A2, B2);
  and and_4 (Y3, A3, B3);
  and and_5 (Y4, A4, B4);
  and and_6 (Y5, A5, B5);
  and and_7 (Y6, A6, B6);
  and and_8 (Y7, A7, B7);
endmodule

module LOGIC_Or (
  input  A0,
  input  B0,
  input  A1,
  input  B1,
  input  A2,
  input  B2,
  input  A3,
  input  B3,
  input  A4,
  input  B4,
  input  A5,
  input  B5,
  input  A6,
  input  B6,
  input  A7,
  input  B7,
  output Y0,
  output Y1,
  output Y2,
  output Y3,
  output Y4,
  output Y5,
  output Y6,
  output Y7
);

  or or_1 (Y0, A0, B0);
  or or_2 (Y1, A1, B1);
  or or_3 (Y2, A2, B2);
  or or_4 (Y3, A3, B3);
  or or_5 (Y4, A4, B4);
  or or_6 (Y5, A5, B5);
  or or_7 (Y6, A6, B6);
  or or_8 (Y7, A7, B7);
endmodule

module LOGIC_Xor (
  input  A0,
  input  B0,
  input  A1,
  input  B1,
  input  A2,
  input  B2,
  input  A3,
  input  B3,
  input  A4,
  input  B4,
  input  A5,
  input  B5,
  input  A6,
  input  B6,
  input  A7,
  input  B7,
  output Y0,
  output Y1,
  output Y2,
  output Y3,
  output Y4,
  output Y5,
  output Y6,
  output Y7
);

  xor xor_1 (Y0, A0, B0);
  xor xor_2 (Y1, A1, B1);
  xor xor_3 (Y2, A2, B2);
  xor xor_4 (Y3, A3, B3);
  xor xor_5 (Y4, A4, B4);
  xor xor_6 (Y5, A5, B5);
  xor xor_7 (Y6, A6, B6);
  xor xor_8 (Y7, A7, B7);
endmodule

module ALU_Arithmetic (
  input  A0,
  input  A1,
  input  A2,
  input  A3,
  input  A4,
  input  A5,
  input  A6,
  input  A7,
  input  B0,
  input  B1,
  input  B2,
  input  B3,
  input  B4,
  input  B5,
  input  B6,
  input  B7,
  input  C0,
  input  C1,
  output Y0,
  output Y1,
  output Y2,
  output Y3,
  output Y4,
  output Y5,
  output Y6,
  output Y7,
  output OVERFLOW
);

  wire arithmetic_addersubtractor_1_overflow, arithmetic_addersubtractor_1_y0,
       arithmetic_addersubtractor_1_y1, arithmetic_addersubtractor_1_y2, arithmetic_addersubtractor_1_y3,
       arithmetic_addersubtractor_1_y4, arithmetic_addersubtractor_1_y5, arithmetic_addersubtractor_1_y6,
       arithmetic_addersubtractor_1_y7, arithmetic_addersubtractor_2_overflow,
       arithmetic_addersubtractor_2_y0, arithmetic_addersubtractor_2_y1, arithmetic_addersubtractor_2_y2,
       arithmetic_addersubtractor_2_y3, arithmetic_addersubtractor_2_y4, arithmetic_addersubtractor_2_y5,
       arithmetic_addersubtractor_2_y6, arithmetic_addersubtractor_2_y7, arithmetic_divider_1_overflow,
       arithmetic_divider_1_y0, arithmetic_divider_1_y1, arithmetic_divider_1_y2, arithmetic_divider_1_y3,
       arithmetic_divider_1_y4, arithmetic_divider_1_y5, arithmetic_divider_1_y6, arithmetic_divider_1_y7,
       arithmetic_multiplier_1_overflow, arithmetic_multiplier_1_y0, arithmetic_multiplier_1_y1,
       arithmetic_multiplier_1_y2, arithmetic_multiplier_1_y3, arithmetic_multiplier_1_y4,
       arithmetic_multiplier_1_y5, arithmetic_multiplier_1_y6, arithmetic_multiplier_1_y7;

  ARITHMETIC_AdderSubtractor arithmetic_addersubtractor_1 (
    .SUB(1'b0), .A0(A0), .A1(A1), .A2(A2), .A3(A3), .A4(A4), .A5(A5), .A6(A6), .A7(A7), .B0(B0), .B1(B1),
    .B2(B2), .B3(B3), .B4(B4), .B5(B5), .B6(B6), .B7(B7), .Y0(arithmetic_addersubtractor_1_y0),
    .Y1(arithmetic_addersubtractor_1_y1), .Y2(arithmetic_addersubtractor_1_y2),
    .Y3(arithmetic_addersubtractor_1_y3), .Y4(arithmetic_addersubtractor_1_y4),
    .Y5(arithmetic_addersubtractor_1_y5), .Y6(arithmetic_addersubtractor_1_y6),
    .Y7(arithmetic_addersubtractor_1_y7), .OVERFLOW(arithmetic_addersubtractor_1_overflow));
  ARITHMETIC_AdderSubtractor arithmetic_addersubtractor_2 (
    .SUB(1'b1), .A0(A0), .A1(A1), .A2(A2), .A3(A3), .A4(A4), .A5(A5), .A6(A6), .A7(A7), .B0(B0), .B1(B1),
    .B2(B2), .B3(B3), .B4(B4), .B5(B5), .B6(B6), .B7(B7), .Y0(arithmetic_addersubtractor_2_y0),
    .Y1(arithmetic_addersubtractor_2_y1), .Y2(arithmetic_addersubtractor_2_y2),
    .Y3(arithmetic_addersubtractor_2_y3), .Y4(arithmetic_addersubtractor_2_y4),
    .Y5(arithmetic_addersubtractor_2_y5), .Y6(arithmetic_addersubtractor_2_y6),
    .Y7(arithmetic_addersubtractor_2_y7), .OVERFLOW(arithmetic_addersubtractor_2_overflow));
  ARITHMETIC_Multiplier arithmetic_multiplier_1 (
    .A0(A0), .A1(A1), .A2(A2), .A3(A3), .A4(A4), .A5(A5), .A6(A6), .A7(A7), .B0(B0), .B1(B1), .B2(B2),
    .B3(B3), .B4(B4), .B5(B5), .B6(B6), .B7(B7), .Y0(arithmetic_multiplier_1_y0),
    .Y1(arithmetic_multiplier_1_y1), .Y2(arithmetic_multiplier_1_y2), .Y3(arithmetic_multiplier_1_y3),
    .Y4(arithmetic_multiplier_1_y4), .Y5(arithmetic_multiplier_1_y5), .Y6(arithmetic_multiplier_1_y6),
    .Y7(arithmetic_multiplier_1_y7), .OVERFLOW(arithmetic_multiplier_1_overflow));
  ARITHMETIC_Divider arithmetic_divider_1 (
    .A0(A0), .A1(A1), .A2(A2), .A3(A3), .A4(A4), .A5(A5), .A6(A6), .A7(A7), .B0(B0), .B1(B1), .B2(B2),
    .B3(B3), .B4(B4), .B5(B5), .B6(B6), .B7(B7), .Y0(arithmetic_divider_1_y0), .Y1(arithmetic_divider_1_y1),
    .Y2(arithmetic_divider_1_y2), .Y3(arithmetic_divider_1_y3), .Y4(arithmetic_divider_1_y4),
    .Y5(arithmetic_divider_1_y5), .Y6(arithmetic_divider_1_y6), .Y7(arithmetic_divider_1_y7),
    .OVERFLOW(arithmetic_divider_1_overflow));
  Multiplexer_x4 multiplexer_x4_1 (
    .C0(C0), .C1(C1), .D0(arithmetic_addersubtractor_1_y0), .D1(arithmetic_addersubtractor_2_y0),
    .D2(arithmetic_multiplier_1_y0), .D3(arithmetic_divider_1_y0), .Y(Y0));
  Multiplexer_x4 multiplexer_x4_2 (
    .C0(C0), .C1(C1), .D0(arithmetic_addersubtractor_1_y1), .D1(arithmetic_addersubtractor_2_y1),
    .D2(arithmetic_multiplier_1_y1), .D3(arithmetic_divider_1_y1), .Y(Y1));
  Multiplexer_x4 multiplexer_x4_3 (
    .C0(C0), .C1(C1), .D0(arithmetic_addersubtractor_1_y2), .D1(arithmetic_addersubtractor_2_y2),
    .D2(arithmetic_multiplier_1_y2), .D3(arithmetic_divider_1_y2), .Y(Y2));
  Multiplexer_x4 multiplexer_x4_4 (
    .C0(C0), .C1(C1), .D0(arithmetic_addersubtractor_1_y3), .D1(arithmetic_addersubtractor_2_y3),
    .D2(arithmetic_multiplier_1_y3), .D3(arithmetic_divider_1_y3), .Y(Y3));
  Multiplexer_x4 multiplexer_x4_5 (
    .C0(C0), .C1(C1), .D0(arithmetic_addersubtractor_1_y4), .D1(arithmetic_addersubtractor_2_y4),
    .D2(arithmetic_multiplier_1_y4), .D3(arithmetic_divider_1_y4), .Y(Y4));
  Multiplexer_x4 multiplexer_x4_6 (
    .C0(C0), .C1(C1), .D0(arithmetic_addersubtractor_1_y5), .D1(arithmetic_addersubtractor_2_y5),
    .D2(arithmetic_multiplier_1_y5), .D3(arithmetic_divider_1_y5), .Y(Y5));
  Multiplexer_x4 multiplexer_x4_7 (
    .C0(C0), .C1(C1), .D0(arithmetic_addersubtractor_1_y6), .D1(arithmetic_addersubtractor_2_y6),
    .D2(arithmetic_multiplier_1_y6), .D3(arithmetic_divider_1_y6), .Y(Y6));
  Multiplexer_x4 multiplexer_x4_8 (
    .C0(C0), .C1(C1), .D0(arithmetic_addersubtractor_1_y7), .D1(arithmetic_addersubtractor_2_y7),
    .D2(arithmetic_multiplier_1_y7), .D3(arithmetic_divider_1_y7), .Y(Y7));
  Multiplexer_x4 multiplexer_x4_9 (
    .C0(C0), .C1(C1), .D0(arithmetic_addersubtractor_1_overflow), .D1(arithmetic_addersubtractor_2_overflow),
    .D2(arithmetic_multiplier_1_overflow), .D3(arithmetic_divider_1_overflow), .Y(OVERFLOW));
endmodule

module ARITHMETIC_AdderSubtractor (
  input  SUB,
  input  A0,
  input  A1,
  input  A2,
  input  A3,
  input  A4,
  input  A5,
  input  A6,
  input  A7,
  input  B0,
  input  B1,
  input  B2,
  input  B3,
  input  B4,
  input  B5,
  input  B6,
  input  B7,
  output Y0,
  output Y1,
  output Y2,
  output Y3,
  output Y4,
  output Y5,
  output Y6,
  output Y7,
  output OVERFLOW
);

  wire and_1_out, and_2_out, and_3_out, and_4_out, and_5_out, and_6_out, and_7_out, and_8_out, and_9_out,
       and_10_out, and_11_out, and_12_out, and_13_out, and_14_out, and_15_out, and_16_out, not_1_out,
       not_2_out, not_3_out, or_1_out, or_2_out, or_3_out, or_4_out, or_5_out, or_6_out, or_7_out, xor_1_out,
       xor_2_out, xor_3_out, xor_4_out, xor_5_out, xor_6_out, xor_7_out, xor_8_out, xor_9_out, xor_10_out,
       xor_11_out, xor_12_out, xor_13_out, xor_14_out, xor_15_out, xor_16_out, xor_17_out;

  xor xor_1 (xor_1_out, B7, SUB);
  xor xor_2 (xor_2_out, B0, SUB);
  xor xor_3 (xor_3_out, B1, SUB);
  xor xor_4 (xor_4_out, B2, SUB);
  xor xor_5 (xor_5_out, B3, SUB);
  xor xor_6 (xor_6_out, B4, SUB);
  xor xor_7 (xor_7_out, B5, SUB);
  xor xor_8 (xor_8_out, B6, SUB);
  xor xor_9 (xor_9_out, B7, SUB);
  not not_1 (not_1_out, xor_1_out);
  not not_2 (not_2_out, A7);
  not not_3 (not_3_out, Y7);
  xor xor_10 (xor_10_out, A0, xor_2_out);
  and and_1 (and_1_out, xor_2_out, A0);
  xor xor_11 (xor_11_out, A1, xor_3_out);
  and and_2 (and_2_out, xor_3_out, A1);
  xor xor_12 (xor_12_out, A2, xor_4_out);
  and and_3 (and_3_out, xor_4_out, A2);
  xor xor_13 (xor_13_out, A3, xor_5_out);
  and and_4 (and_4_out, xor_5_out, A3);
  xor xor_14 (xor_14_out, A4, xor_6_out);
  and and_5 (and_5_out, xor_6_out, A4);
  xor xor_15 (xor_15_out, A5, xor_7_out);
  and and_6 (and_6_out, xor_7_out, A5);
  xor xor_16 (xor_16_out, A6, xor_8_out);
  and and_7 (and_7_out, xor_8_out, A6);
  xor xor_17 (xor_17_out, A7, xor_9_out);
  and and_8 (and_8_out, not_1_out, not_2_out, Y7);
  and and_9 (and_9_out, not_3_out, xor_1_out, A7);
  and and_10 (and_10_out, SUB, xor_10_out);
  or or_1 (or_1_out, and_1_out, and_10_out);
  and and_11 (and_11_out, or_1_out, xor_11_out);
  or or_2 (or_2_out, and_2_out, and_11_out);
  and and_12 (and_12_out, or_2_out, xor_12_out);
  or or_3 (or_3_out, and_3_out, and_12_out);
  and and_13 (and_13_out, or_3_out, xor_13_out);
  or or_4 (or_4_out, and_4_out, and_13_out);
  and and_14 (and_14_out, or_4_out, xor_14_out);
  or or_5 (or_5_out, and_5_out, and_14_out);
  and and_15 (and_15_out, or_5_out, xor_15_out);
  or or_6 (or_6_out, and_6_out, and_15_out);
  and and_16 (and_16_out, or_6_out, xor_16_out);
  or or_7 (or_7_out, and_7_out, and_16_out);
  or or_8 (OVERFLOW, and_8_out, and_9_out);
  xor xor_18 (Y0, SUB, xor_10_out);
  xor xor_19 (Y1, or_1_out, xor_11_out);
  xor xor_20 (Y2, or_2_out, xor_12_out);
  xor xor_21 (Y3, or_3_out, xor_13_out);
  xor xor_22 (Y4, or_4_out, xor_14_out);
  xor xor_23 (Y5, or_5_out, xor_15_out);
  xor xor_24 (Y6, or_6_out, xor_16_out);
  xor xor_25 (Y7, or_7_out, xor_17_out);
endmodule

module ARITHMETIC_Multiplier (
  input  A0,
  input  A1,
  input  A2,
  input  A3,
  input  A4,
  input  A5,
  input  A6,
  input  A7,
  input  B0,
  input  B1,
  input  B2,
  input  B3,
  input  B4,
  input  B5,
  input  B6,
  input  B7,
  output Y0,
  output Y1,
  output Y2,
  output Y3,
  output Y4,
  output Y5,
  output Y6,
  output Y7,
  output OVERFLOW
);

  wire and_2_out, and_3_out, and_4_out, and_5_out, and_6_out, and_7_out, multiplier_partialadder_1_cout,
       multiplier_partialadder_1_xout, multiplier_partialadder_1_yout, multiplier_partialadder_2_cout,
       multiplier_partialadder_2_xout, multiplier_partialadder_2_xyout, multiplier_partialadder_2_yout,
       multiplier_partialadder_3_cout, multiplier_partialadder_3_xout, multiplier_partialadder_3_xyout,
       multiplier_partialadder_3_yout, multiplier_partialadder_4_cout, multiplier_partialadder_4_xout,
       multiplier_partialadder_4_xyout, multiplier_partialadder_4_yout, multiplier_partialadder_5_cout,
       multiplier_partialadder_5_xout, multiplier_partialadder_5_xyout, multiplier_partialadder_5_yout,
       multiplier_partialadder_6_cout, multiplier_partialadder_6_xout, multiplier_partialadder_6_xyout,
       multiplier_partialadder_6_yout, multiplier_partialadder_7_cout, multiplier_partialadder_7_xout,
       multiplier_partialadder_7_xyout, multiplier_partialadder_7_yout, multiplier_partialadder_8_cout,
       multiplier_partialadder_8_xout, multiplier_partialadder_8_yout, multiplier_partialadder_9_cout,
       multiplier_partialadder_9_xout, multiplier_partialadder_9_xyout, multiplier_partialadder_9_yout,
       multiplier_partialadder_10_cout, multiplier_partialadder_10_xout, multiplier_partialadder_10_xyout,
       multiplier_partialadder_10_yout, multiplier_partialadder_11_cout, multiplier_partialadder_11_xout,
       multiplier_partialadder_11_xyout, multiplier_partialadder_11_yout, multiplier_partialadder_12_cout,
       multiplier_partialadder_12_xout, multiplier_partialadder_12_xyout, multiplier_partialadder_12_yout,
       multiplier_partialadder_13_cout, multiplier_partialadder_13_xout, multiplier_partialadder_13_xyout,
       multiplier_partialadder_13_yout, multiplier_partialadder_14_cout, multiplier_partialadder_14_xout,
       multiplier_partialadder_14_xyout, multiplier_partialadder_14_yout, multiplier_partialadder_15_cout,
       multiplier_partialadder_15_xout, multiplier_partialadder_15_yout, multiplier_partialadder_16_cout,
       multiplier_partialadder_16_xout, multiplier_partialadder_16_xyout, multiplier_partialadder_16_yout,
       multiplier_partialadder_17_cout, multiplier_partialadder_17_xout, multiplier_partialadder_17_xyout,
       multiplier_partialadder_17_yout, multiplier_partialadder_18_cout, multiplier_partialadder_18_xout,
       multiplier_partialadder_18_xyout, multiplier_partialadder_18_yout, multiplier_partialadder_19_cout,
       multiplier_partialadder_19_xout, multiplier_partialadder_19_xyout, multiplier_partialadder_19_yout,
       multiplier_partialadder_20_cout, multiplier_partialadder_20_xout, multiplier_partialadder_20_xyout,
       multiplier_partialadder_20_yout, multiplier_partialadder_21_cout, multiplier_partialadder_21_xout,
       multiplier_partialadder_21_xyout, multiplier_partialadder_21_yout, multiplier_partialadder_22_cout,
       multiplier_partialadder_22_xout, multiplier_partialadder_22_yout, multiplier_partialadder_23_cout,
       multiplier_partialadder_23_xout, multiplier_partialadder_23_xyout, multiplier_partialadder_23_yout,
       multiplier_partialadder_24_cout, multiplier_partialadder_24_xout, multiplier_partialadder_24_xyout,
       multiplier_partialadder_24_yout, multiplier_partialadder_25_cout, multiplier_partialadder_25_xout,
       multiplier_partialadder_25_xyout, multiplier_partialadder_25_yout, multiplier_partialadder_26_cout,
       multiplier_partialadder_26_xout, multiplier_partialadder_26_xyout, multiplier_partialadder_26_yout,
       multiplier_partialadder_27_cout, multiplier_partialadder_27_xout, multiplier_partialadder_27_xyout,
       multiplier_partialadder_27_yout, multiplier_partialadder_28_cout, multiplier_partialadder_28_xout,
       multiplier_partialadder_28_xyout, multiplier_partialadder_28_yout, multiplier_partialadder_29_cout,
       multiplier_partialadder_29_xout, multiplier_partialadder_29_yout, multiplier_partialadder_30_cout,
       multiplier_partialadder_30_xout, multiplier_partialadder_30_xyout, multiplier_partialadder_30_yout,
       multiplier_partialadder_31_cout, multiplier_partialadder_31_xout, multiplier_partialadder_31_xyout,
       multiplier_partialadder_31_yout, multiplier_partialadder_32_cout, multiplier_partialadder_32_xout,
       multiplier_partialadder_32_xyout, multiplier_partialadder_32_yout, multiplier_partialadder_33_cout,
       multiplier_partialadder_33_xout, multiplier_partialadder_33_xyout, multiplier_partialadder_33_yout,
       multiplier_partialadder_34_cout, multiplier_partialadder_34_xout, multiplier_partialadder_34_xyout,
       multiplier_partialadder_34_yout, multiplier_partialadder_35_cout, multiplier_partialadder_35_xout,
       multiplier_partialadder_35_xyout, multiplier_partialadder_35_yout, multiplier_partialadder_36_cout,
       multiplier_partialadder_36_xout, multiplier_partialadder_36_yout, multiplier_partialadder_37_cout,
       multiplier_partialadder_37_xout, multiplier_partialadder_37_xyout, multiplier_partialadder_37_yout,
       multiplier_partialadder_38_cout, multiplier_partialadder_38_xout, multiplier_partialadder_38_xyout,
       multiplier_partialadder_38_yout, multiplier_partialadder_39_cout, multiplier_partialadder_39_xout,
       multiplier_partialadder_39_xyout, multiplier_partialadder_39_yout, multiplier_partialadder_40_cout,
       multiplier_partialadder_40_xout, multiplier_partialadder_40_xyout, multiplier_partialadder_40_yout,
       multiplier_partialadder_41_cout, multiplier_partialadder_41_xout, multiplier_partialadder_41_xyout,
       multiplier_partialadder_41_yout, multiplier_partialadder_42_cout, multiplier_partialadder_42_xout,
       multiplier_partialadder_42_xyout, multiplier_partialadder_42_yout, multiplier_partialadder_43_cout,
       multiplier_partialadder_43_xyout, multiplier_partialadder_44_xyout, multiplier_partialaddernot_1_cout,
       multiplier_partialaddernot_1_xout, multiplier_partialaddernot_1_xyout,
       multiplier_partialaddernot_2_cout, multiplier_partialaddernot_2_xout,
       multiplier_partialaddernot_2_xyout, multiplier_partialaddernot_3_cout,
       multiplier_partialaddernot_3_xout, multiplier_partialaddernot_3_xyout,
       multiplier_partialaddernot_4_cout, multiplier_partialaddernot_4_xout,
       multiplier_partialaddernot_4_xyout, multiplier_partialaddernot_5_cout,
       multiplier_partialaddernot_5_xout, multiplier_partialaddernot_5_xyout,
       multiplier_partialaddernot_6_cout, multiplier_partialaddernot_6_xout,
       multiplier_partialaddernot_6_xyout, multiplier_partialaddernot_7_cout,
       multiplier_partialaddernot_7_yout, multiplier_partialaddernot_8_cout,
       multiplier_partialaddernot_8_xyout, multiplier_partialaddernot_8_yout,
       multiplier_partialaddernot_9_cout, multiplier_partialaddernot_9_xyout,
       multiplier_partialaddernot_9_yout, multiplier_partialaddernot_10_cout,
       multiplier_partialaddernot_10_xyout, multiplier_partialaddernot_10_yout,
       multiplier_partialaddernot_11_cout, multiplier_partialaddernot_11_xyout,
       multiplier_partialaddernot_11_yout, multiplier_partialaddernot_12_cout,
       multiplier_partialaddernot_12_xyout, multiplier_partialaddernot_12_yout,
       multiplier_partialaddernot_13_cout, multiplier_partialaddernot_13_xyout,
       multiplier_partialaddernot_13_yout, nand_1_out, xor_1_out, xor_2_out, xor_3_out, xor_4_out, xor_5_out,
       xor_6_out, xor_7_out, xor_8_out;

  and and_1 (Y0, A0, B0);
  and and_2 (and_2_out, A0, B1);
  and and_3 (and_3_out, A0, B2);
  and and_4 (and_4_out, A0, B3);
  and and_5 (and_5_out, A0, B4);
  and and_6 (and_6_out, A0, B5);
  and and_7 (and_7_out, A0, B6);
  nand nand_1 (nand_1_out, A0, B7);
  MULTIPLIER_PartialAdder multiplier_partialadder_1 (
    .Z(and_2_out), .Xin(B0), .Yin(A1), .Cin(1'b0), .Yout(multiplier_partialadder_1_yout),
    .Cout(multiplier_partialadder_1_cout), .XYout(Y1), .Xout(multiplier_partialadder_1_xout));
  MULTIPLIER_PartialAdder multiplier_partialadder_2 (
    .Z(and_3_out), .Xin(B1), .Yin(multiplier_partialadder_1_yout), .Cin(multiplier_partialadder_1_cout),
    .Yout(multiplier_partialadder_2_yout), .Cout(multiplier_partialadder_2_cout),
    .XYout(multiplier_partialadder_2_xyout), .Xout(multiplier_partialadder_2_xout));
  MULTIPLIER_PartialAdder multiplier_partialadder_3 (
    .Z(and_4_out), .Xin(B2), .Yin(multiplier_partialadder_2_yout), .Cin(multiplier_partialadder_2_cout),
    .Yout(multiplier_partialadder_3_yout), .Cout(multiplier_partialadder_3_cout),
    .XYout(multiplier_partialadder_3_xyout), .Xout(multiplier_partialadder_3_xout));
  MULTIPLIER_PartialAdder multiplier_partialadder_4 (
    .Z(and_5_out), .Xin(B3), .Yin(multiplier_partialadder_3_yout), .Cin(multiplier_partialadder_3_cout),
    .Yout(multiplier_partialadder_4_yout), .Cout(multiplier_partialadder_4_cout),
    .XYout(multiplier_partialadder_4_xyout), .Xout(multiplier_partialadder_4_xout));
  MULTIPLIER_PartialAdder multiplier_partialadder_5 (
    .Z(and_6_out), .Xin(B4), .Yin(multiplier_partialadder_4_yout), .Cin(multiplier_partialadder_4_cout),
    .Yout(multiplier_partialadder_5_yout), .Cout(multiplier_partialadder_5_cout),
    .XYout(multiplier_partialadder_5_xyout), .Xout(multiplier_partialadder_5_xout));
  MULTIPLIER_PartialAdder multiplier_partialadder_6 (
    .Z(and_7_out), .Xin(B5), .Yin(multiplier_partialadder_5_yout), .Cin(multiplier_partialadder_5_cout),
    .Yout(multiplier_partialadder_6_yout), .Cout(multiplier_partialadder_6_cout),
    .XYout(multiplier_partialadder_6_xyout), .Xout(multiplier_partialadder_6_xout));
  MULTIPLIER_PartialAdder multiplier_partialadder_7 (
    .Z(nand_1_out), .Xin(B6), .Yin(multiplier_partialadder_6_yout), .Cin(multiplier_partialadder_6_cout),
    .Yout(multiplier_partialadder_7_yout), .Cout(multiplier_partialadder_7_cout),
    .XYout(multiplier_partialadder_7_xyout), .Xout(multiplier_partialadder_7_xout));
  MULTIPLIER_PartialAdderNot multiplier_partialaddernot_1 (
    .Z(1'b1), .Xin(B7), .Yin(multiplier_partialadder_7_yout), .Cin(multiplier_partialadder_7_cout),
    .Cout(multiplier_partialaddernot_1_cout), .XYout(multiplier_partialaddernot_1_xyout),
    .Xout(multiplier_partialaddernot_1_xout));  // open: Yout
  MULTIPLIER_PartialAdder multiplier_partialadder_8 (
    .Z(multiplier_partialadder_2_xyout), .Xin(multiplier_partialadder_1_xout), .Yin(A2), .Cin(1'b0),
    .Yout(multiplier_partialadder_8_yout), .Cout(multiplier_partialadder_8_cout), .XYout(Y2),
    .Xout(multiplier_partialadder_8_xout));
  MULTIPLIER_PartialAdder multiplier_partialadder_9 (
    .Z(multiplier_partialadder_3_xyout), .Xin(multiplier_partialadder_2_xout),
    .Yin(multiplier_partialadder_8_yout), .Cin(multiplier_partialadder_8_cout),
    .Yout(multiplier_partialadder_9_yout), .Cout(multiplier_partialadder_9_cout),
    .XYout(multiplier_partialadder_9_xyout), .Xout(multiplier_partialadder_9_xout));
  MULTIPLIER_PartialAdder multiplier_partialadder_10 (
    .Z(multiplier_partialadder_4_xyout), .Xin(multiplier_partialadder_3_xout),
    .Yin(multiplier_partialadder_9_yout), .Cin(multiplier_partialadder_9_cout),
    .Yout(multiplier_partialadder_10_yout), .Cout(multiplier_partialadder_10_cout),
    .XYout(multiplier_partialadder_10_xyout), .Xout(multiplier_partialadder_10_xout));
  MULTIPLIER_PartialAdder multiplier_partialadder_11 (
    .Z(multiplier_partialadder_5_xyout), .Xin(multiplier_partialadder_4_xout),
    .Yin(multiplier_partialadder_10_yout), .Cin(multiplier_partialadder_10_cout),
    .Yout(multiplier_partialadder_11_yout), .Cout(multiplier_partialadder_11_cout),
    .XYout(multiplier_partialadder_11_xyout), .Xout(multiplier_partialadder_11_xout));
  MULTIPLIER_PartialAdder multiplier_partialadder_12 (
    .Z(multiplier_partialadder_6_xyout), .Xin(multiplier_partialadder_5_xout),
    .Yin(multiplier_partialadder_11_yout), .Cin(multiplier_partialadder_11_cout),
    .Yout(multiplier_partialadder_12_yout), .Cout(multiplier_partialadder_12_cout),
    .XYout(multiplier_partialadder_12_xyout), .Xout(multiplier_partialadder_12_xout));
  MULTIPLIER_PartialAdder multiplier_partialadder_13 (
    .Z(multiplier_partialadder_7_xyout), .Xin(multiplier_partialadder_6_xout),
    .Yin(multiplier_partialadder_12_yout), .Cin(multiplier_partialadder_12_cout),
    .Yout(multiplier_partialadder_13_yout), .Cout(multiplier_partialadder_13_cout),
    .XYout(multiplier_partialadder_13_xyout), .Xout(multiplier_partialadder_13_xout));
  MULTIPLIER_PartialAdder multiplier_partialadder_14 (
    .Z(multiplier_partialaddernot_1_xyout), .Xin(multiplier_partialadder_7_xout),
    .Yin(multiplier_partialadder_13_yout), .Cin(multiplier_partialadder_13_cout),
    .Yout(multiplier_partialadder_14_yout), .Cout(multiplier_partialadder_14_cout),
    .XYout(multiplier_partialadder_14_xyout), .Xout(multiplier_partialadder_14_xout));
  MULTIPLIER_PartialAdderNot multiplier_partialaddernot_2 (
    .Z(multiplier_partialaddernot_1_cout), .Xin(multiplier_partialaddernot_1_xout),
    .Yin(multiplier_partialadder_14_yout), .Cin(multiplier_partialadder_14_cout),
    .Cout(multiplier_partialaddernot_2_cout), .XYout(multiplier_partialaddernot_2_xyout),
    .Xout(multiplier_partialaddernot_2_xout));  // open: Yout
  MULTIPLIER_PartialAdder multiplier_partialadder_15 (
    .Z(multiplier_partialadder_9_xyout), .Xin(multiplier_partialadder_8_xout), .Yin(A3), .Cin(1'b0),
    .Yout(multiplier_partialadder_15_yout), .Cout(multiplier_partialadder_15_cout), .XYout(Y3),
    .Xout(multiplier_partialadder_15_xout));
  MULTIPLIER_PartialAdder multiplier_partialadder_16 (
    .Z(multiplier_partialadder_10_xyout), .Xin(multiplier_partialadder_9_xout),
    .Yin(multiplier_partialadder_15_yout), .Cin(multiplier_partialadder_15_cout),
    .Yout(multiplier_partialadder_16_yout), .Cout(multiplier_partialadder_16_cout),
    .XYout(multiplier_partialadder_16_xyout), .Xout(multiplier_partialadder_16_xout));
  MULTIPLIER_PartialAdder multiplier_partialadder_17 (
    .Z(multiplier_partialadder_11_xyout), .Xin(multiplier_partialadder_10_xout),
    .Yin(multiplier_partialadder_16_yout), .Cin(multiplier_partialadder_16_cout),
    .Yout(multiplier_partialadder_17_yout), .Cout(multiplier_partialadder_17_cout),
    .XYout(multiplier_partialadder_17_xyout), .Xout(multiplier_partialadder_17_xout));
  MULTIPLIER_PartialAdder multiplier_partialadder_18 (
    .Z(multiplier_partialadder_12_xyout), .Xin(multiplier_partialadder_11_xout),
    .Yin(multiplier_partialadder_17_yout), .Cin(multiplier_partialadder_17_cout),
    .Yout(multiplier_partialadder_18_yout), .Cout(multiplier_partialadder_18_cout),
    .XYout(multiplier_partialadder_18_xyout), .Xout(multiplier_partialadder_18_xout));
  MULTIPLIER_PartialAdder multiplier_partialadder_19 (
    .Z(multiplier_partialadder_13_xyout), .Xin(multiplier_partialadder_12_xout),
    .Yin(multiplier_partialadder_18_yout), .Cin(multiplier_partialadder_18_cout),
    .Yout(multiplier_partialadder_19_yout), .Cout(multiplier_partialadder_19_cout),
    .XYout(multiplier_partialadder_19_xyout), .Xout(multiplier_partialadder_19_xout));
  MULTIPLIER_PartialAdder multiplier_partialadder_20 (
    .Z(multiplier_partialadder_14_xyout), .Xin(multiplier_partialadder_13_xout),
    .Yin(multiplier_partialadder_19_yout), .Cin(multiplier_partialadder_19_cout),
    .Yout(multiplier_partialadder_20_yout), .Cout(multiplier_partialadder_20_cout),
    .XYout(multiplier_partialadder_20_xyout), .Xout(multiplier_partialadder_20_xout));
  MULTIPLIER_PartialAdder multiplier_partialadder_21 (
    .Z(multiplier_partialaddernot_2_xyout), .Xin(multiplier_partialadder_14_xout),
    .Yin(multiplier_partialadder_20_yout), .Cin(multiplier_partialadder_20_cout),
    .Yout(multiplier_partialadder_21_yout), .Cout(multiplier_partialadder_21_cout),
    .XYout(multiplier_partialadder_21_xyout), .Xout(multiplier_partialadder_21_xout));
  MULTIPLIER_PartialAdderNot multiplier_partialaddernot_3 (
    .Z(multiplier_partialaddernot_2_cout), .Xin(multiplier_partialaddernot_2_xout),
    .Yin(multiplier_partialadder_21_yout), .Cin(multiplier_partialadder_21_cout),
    .Cout(multiplier_partialaddernot_3_cout), .XYout(multiplier_partialaddernot_3_xyout),
    .Xout(multiplier_partialaddernot_3_xout));  // open: Yout
  MULTIPLIER_PartialAdder multiplier_partialadder_22 (
    .Z(multiplier_partialadder_16_xyout), .Xin(multiplier_partialadder_15_xout), .Yin(A4), .Cin(1'b0),
    .Yout(multiplier_partialadder_22_yout), .Cout(multiplier_partialadder_22_cout), .XYout(Y4),
    .Xout(multiplier_partialadder_22_xout));
  MULTIPLIER_PartialAdder multiplier_partialadder_23 (
    .Z(multiplier_partialadder_17_xyout), .Xin(multiplier_partialadder_16_xout),
    .Yin(multiplier_partialadder_22_yout), .Cin(multiplier_partialadder_22_cout),
    .Yout(multiplier_partialadder_23_yout), .Cout(multiplier_partialadder_23_cout),
    .XYout(multiplier_partialadder_23_xyout), .Xout(multiplier_partialadder_23_xout));
  MULTIPLIER_PartialAdder multiplier_partialadder_24 (
    .Z(multiplier_partialadder_18_xyout), .Xin(multiplier_partialadder_17_xout),
    .Yin(multiplier_partialadder_23_yout), .Cin(multiplier_partialadder_23_cout),
    .Yout(multiplier_partialadder_24_yout), .Cout(multiplier_partialadder_24_cout),
    .XYout(multiplier_partialadder_24_xyout), .Xout(multiplier_partialadder_24_xout));
  MULTIPLIER_PartialAdder multiplier_partialadder_25 (
    .Z(multiplier_partialadder_19_xyout), .Xin(multiplier_partialadder_18_xout),
    .Yin(multiplier_partialadder_24_yout), .Cin(multiplier_partialadder_24_cout),
    .Yout(multiplier_partialadder_25_yout), .Cout(multiplier_partialadder_25_cout),
    .XYout(multiplier_partialadder_25_xyout), .Xout(multiplier_partialadder_25_xout));
  MULTIPLIER_PartialAdder multiplier_partialadder_26 (
    .Z(multiplier_partialadder_20_xyout), .Xin(multiplier_partialadder_19_xout),
    .Yin(multiplier_partialadder_25_yout), .Cin(multiplier_partialadder_25_cout),
    .Yout(multiplier_partialadder_26_yout), .Cout(multiplier_partialadder_26_cout),
    .XYout(multiplier_partialadder_26_xyout), .Xout(multiplier_partialadder_26_xout));
  MULTIPLIER_PartialAdder multiplier_partialadder_27 (
    .Z(multiplier_partialadder_21_xyout), .Xin(multiplier_partialadder_20_xout),
    .Yin(multiplier_partialadder_26_yout), .Cin(multiplier_partialadder_26_cout),
    .Yout(multiplier_partialadder_27_yout), .Cout(multiplier_partialadder_27_cout),
    .XYout(multiplier_partialadder_27_xyout), .Xout(multiplier_partialadder_27_xout));
  MULTIPLIER_PartialAdder multiplier_partialadder_28 (
    .Z(multiplier_partialaddernot_3_xyout), .Xin(multiplier_partialadder_21_xout),
    .Yin(multiplier_partialadder_27_yout), .Cin(multiplier_partialadder_27_cout),
    .Yout(multiplier_partialadder_28_yout), .Cout(multiplier_partialadder_28_cout),
    .XYout(multiplier_partialadder_28_xyout), .Xout(multiplier_partialadder_28_xout));
  MULTIPLIER_PartialAdderNot multiplier_partialaddernot_4 (
    .Z(multiplier_partialaddernot_3_cout), .Xin(multiplier_partialaddernot_3_xout),
    .Yin(multiplier_partialadder_28_yout), .Cin(multiplier_partialadder_28_cout),
    .Cout(multiplier_partialaddernot_4_cout), .XYout(multiplier_partialaddernot_4_xyout),
    .Xout(multiplier_partialaddernot_4_xout));  // open: Yout
  MULTIPLIER_PartialAdder multiplier_partialadder_29 (
    .Z(multiplier_partialadder_23_xyout), .Xin(multiplier_partialadder_22_xout), .Yin(A5), .Cin(1'b0),
    .Yout(multiplier_partialadder_29_yout), .Cout(multiplier_partialadder_29_cout), .XYout(Y5),
    .Xout(multiplier_partialadder_29_xout));
  MULTIPLIER_PartialAdder multiplier_partialadder_30 (
    .Z(multiplier_partialadder_24_xyout), .Xin(multiplier_partialadder_23_xout),
    .Yin(multiplier_partialadder_29_yout), .Cin(multiplier_partialadder_29_cout),
    .Yout(multiplier_partialadder_30_yout), .Cout(multiplier_partialadder_30_cout),
    .XYout(multiplier_partialadder_30_xyout), .Xout(multiplier_partialadder_30_xout));
  MULTIPLIER_PartialAdder multiplier_partialadder_31 (
    .Z(multiplier_partialadder_25_xyout), .Xin(multiplier_partialadder_24_xout),
    .Yin(multiplier_partialadder_30_yout), .Cin(multiplier_partialadder_30_cout),
    .Yout(multiplier_partialadder_31_yout), .Cout(multiplier_partialadder_31_cout),
    .XYout(multiplier_partialadder_31_xyout), .Xout(multiplier_partialadder_31_xout));
  MULTIPLIER_PartialAdder multiplier_partialadder_32 (
    .Z(multiplier_partialadder_26_xyout), .Xin(multiplier_partialadder_25_xout),
    .Yin(multiplier_partialadder_31_yout), .Cin(multiplier_partialadder_31_cout),
    .Yout(multiplier_partialadder_32_yout), .Cout(multiplier_partialadder_32_cout),
    .XYout(multiplier_partialadder_32_xyout), .Xout(multiplier_partialadder_32_xout));
  MULTIPLIER_PartialAdder multiplier_partialadder_33 (
    .Z(multiplier_partialadder_27_xyout), .Xin(multiplier_partialadder_26_xout),
    .Yin(multiplier_partialadder_32_yout), .Cin(multiplier_partialadder_32_cout),
    .Yout(multiplier_partialadder_33_yout), .Cout(multiplier_partialadder_33_cout),
    .XYout(multiplier_partialadder_33_xyout), .Xout(multiplier_partialadder_33_xout));
  MULTIPLIER_PartialAdder multiplier_partialadder_34 (
    .Z(multiplier_partialadder_28_xyout), .Xin(multiplier_partialadder_27_xout),
    .Yin(multiplier_partialadder_33_yout), .Cin(multiplier_partialadder_33_cout),
    .Yout(multiplier_partialadder_34_yout), .Cout(multiplier_partialadder_34_cout),
    .XYout(multiplier_partialadder_34_xyout), .Xout(multiplier_partialadder_34_xout));
  MULTIPLIER_PartialAdder multiplier_partialadder_35 (
    .Z(multiplier_partialaddernot_4_xyout), .Xin(multiplier_partialadder_28_xout),
    .Yin(multiplier_partialadder_34_yout), .Cin(multiplier_partialadder_34_cout),
    .Yout(multiplier_partialadder_35_yout), .Cout(multiplier_partialadder_35_cout),
    .XYout(multiplier_partialadder_35_xyout), .Xout(multiplier_partialadder_35_xout));
  MULTIPLIER_PartialAdderNot multiplier_partialaddernot_5 (
    .Z(multiplier_partialaddernot_4_cout), .Xin(multiplier_partialaddernot_4_xout),
    .Yin(multiplier_partialadder_35_yout), .Cin(multiplier_partialadder_35_cout),
    .Cout(multiplier_partialaddernot_5_cout), .XYout(multiplier_partialaddernot_5_xyout),
    .Xout(multiplier_partialaddernot_5_xout));  // open: Yout
  MULTIPLIER_PartialAdder multiplier_partialadder_36 (
    .Z(multiplier_partialadder_30_xyout), .Xin(multiplier_partialadder_29_xout), .Yin(A6), .Cin(1'b0),
    .Yout(multiplier_partialadder_36_yout), .Cout(multiplier_partialadder_36_cout), .XYout(Y6),
    .Xout(multiplier_partialadder_36_xout));
  MULTIPLIER_PartialAdder multiplier_partialadder_37 (
    .Z(multiplier_partialadder_31_xyout), .Xin(multiplier_partialadder_30_xout),
    .Yin(multiplier_partialadder_36_yout), .Cin(multiplier_partialadder_36_cout),
    .Yout(multiplier_partialadder_37_yout), .Cout(multiplier_partialadder_37_cout),
    .XYout(multiplier_partialadder_37_xyout), .Xout(multiplier_partialadder_37_xout));
  MULTIPLIER_PartialAdder multiplier_partialadder_38 (
    .Z(multiplier_partialadder_32_xyout), .Xin(multiplier_partialadder_31_xout),
    .Yin(multiplier_partialadder_37_yout), .Cin(multiplier_partialadder_37_cout),
    .Yout(multiplier_partialadder_38_yout), .Cout(multiplier_partialadder_38_cout),
    .XYout(multiplier_partialadder_38_xyout), .Xout(multiplier_partialadder_38_xout));
  MULTIPLIER_PartialAdder multiplier_partialadder_39 (
    .Z(multiplier_partialadder_33_xyout), .Xin(multiplier_partialadder_32_xout),
    .Yin(multiplier_partialadder_38_yout), .Cin(multiplier_partialadder_38_cout),
    .Yout(multiplier_partialadder_39_yout), .Cout(multiplier_partialadder_39_cout),
    .XYout(multiplier_partialadder_39_xyout), .Xout(multiplier_partialadder_39_xout));
  MULTIPLIER_PartialAdder multiplier_partialadder_40 (
    .Z(multiplier_partialadder_34_xyout), .Xin(multiplier_partialadder_33_xout),
    .Yin(multiplier_partialadder_39_yout), .Cin(multiplier_partialadder_39_cout),
    .Yout(multiplier_partialadder_40_yout), .Cout(multiplier_partialadder_40_cout),
    .XYout(multiplier_partialadder_40_xyout), .Xout(multiplier_partialadder_40_xout));
  MULTIPLIER_PartialAdder multiplier_partialadder_41 (
    .Z(multiplier_partialadder_35_xyout), .Xin(multiplier_partialadder_34_xout),
    .Yin(multiplier_partialadder_40_yout), .Cin(multiplier_partialadder_40_cout),
    .Yout(multiplier_partialadder_41_yout), .Cout(multiplier_partialadder_41_cout),
    .XYout(multiplier_partialadder_41_xyout), .Xout(multiplier_partialadder_41_xout));
  MULTIPLIER_PartialAdder multiplier_partialadder_42 (
    .Z(multiplier_partialaddernot_5_xyout), .Xin(multiplier_partialadder_35_xout),
    .Yin(multiplier_partialadder_41_yout), .Cin(multiplier_partialadder_41_cout),
    .Yout(multiplier_partialadder_42_yout), .Cout(multiplier_partialadder_42_cout),
    .XYout(multiplier_partialadder_42_xyout), .Xout(multiplier_partialadder_42_xout));
  MULTIPLIER_PartialAdderNot multiplier_partialaddernot_6 (
    .Z(multiplier_partialaddernot_5_cout), .Xin(multiplier_partialaddernot_5_xout),
    .Yin(multiplier_partialadder_42_yout), .Cin(multiplier_partialadder_42_cout),
    .Cout(multiplier_partialaddernot_6_cout), .XYout(multiplier_partialaddernot_6_xyout),
    .Xout(multiplier_partialaddernot_6_xout));  // open: Yout
  MULTIPLIER_PartialAdderNot multiplier_partialaddernot_7 (
    .Z(multiplier_partialadder_37_xyout), .Xin(multiplier_partialadder_36_xout), .Yin(A7), .Cin(1'b0),
    .Yout(multiplier_partialaddernot_7_yout), .Cout(multiplier_partialaddernot_7_cout), .XYout(Y7));  // open: Xout
  MULTIPLIER_PartialAdderNot multiplier_partialaddernot_8 (
    .Z(multiplier_partialadder_38_xyout), .Xin(multiplier_partialadder_37_xout),
    .Yin(multiplier_partialaddernot_7_yout), .Cin(multiplier_partialaddernot_7_cout),
    .Yout(multiplier_partialaddernot_8_yout), .Cout(multiplier_partialaddernot_8_cout),
    .XYout(multiplier_partialaddernot_8_xyout));  // open: Xout
  MULTIPLIER_PartialAdderNot multiplier_partialaddernot_9 (
    .Z(multiplier_partialadder_39_xyout), .Xin(multiplier_partialadder_38_xout),
    .Yin(multiplier_partialaddernot_8_yout), .Cin(multiplier_partialaddernot_8_cout),
    .Yout(multiplier_partialaddernot_9_yout), .Cout(multiplier_partialaddernot_9_cout),
    .XYout(multiplier_partialaddernot_9_xyout));  // open: Xout
  MULTIPLIER_PartialAdderNot multiplier_partialaddernot_10 (
    .Z(multiplier_partialadder_40_xyout), .Xin(multiplier_partialadder_39_xout),
    .Yin(multiplier_partialaddernot_9_yout), .Cin(multiplier_partialaddernot_9_cout),
    .Yout(multiplier_partialaddernot_10_yout), .Cout(multiplier_partialaddernot_10_cout),
    .XYout(multiplier_partialaddernot_10_xyout));  // open: Xout
  MULTIPLIER_PartialAdderNot multiplier_partialaddernot_11 (
    .Z(multiplier_partialadder_41_xyout), .Xin(multiplier_partialadder_40_xout),
    .Yin(multiplier_partialaddernot_10_yout), .Cin(multiplier_partialaddernot_10_cout),
    .Yout(multiplier_partialaddernot_11_yout), .Cout(multiplier_partialaddernot_11_cout),
    .XYout(multiplier_partialaddernot_11_xyout));  // open: Xout
  MULTIPLIER_PartialAdderNot multiplier_partialaddernot_12 (
    .Z(multiplier_partialadder_42_xyout), .Xin(multiplier_partialadder_41_xout),
    .Yin(multiplier_partialaddernot_11_yout), .Cin(multiplier_partialaddernot_11_cout),
    .Yout(multiplier_partialaddernot_12_yout), .Cout(multiplier_partialaddernot_12_cout),
    .XYout(multiplier_partialaddernot_12_xyout));  // open: Xout
  MULTIPLIER_PartialAdderNot multiplier_partialaddernot_13 (
    .Z(multiplier_partialaddernot_6_xyout), .Xin(multiplier_partialadder_42_xout),
    .Yin(multiplier_partialaddernot_12_yout), .Cin(multiplier_partialaddernot_12_cout),
    .Yout(multiplier_partialaddernot_13_yout), .Cout(multiplier_partialaddernot_13_cout),
    .XYout(multiplier_partialaddernot_13_xyout));  // open: Xout
  MULTIPLIER_PartialAdder multiplier_partialadder_43 (
    .Z(multiplier_partialaddernot_6_cout), .Xin(multiplier_partialaddernot_6_xout),
    .Yin(multiplier_partialaddernot_13_yout), .Cin(multiplier_partialaddernot_13_cout),
    .Cout(multiplier_partialadder_43_cout), .XYout(multiplier_partialadder_43_xyout));  // open: Yout, Xout
  MULTIPLIER_PartialAdder multiplier_partialadder_44 (
    .Z(1'b1), .Xin(1'b0), .Yin(1'b0), .Cin(multiplier_partialadder_43_cout),
    .XYout(multiplier_partialadder_44_xyout));  // open: Yout, Cout, Xout
  xor xor_1 (xor_1_out, multiplier_partialaddernot_8_xyout, Y7);
  xor xor_2 (xor_2_out, multiplier_partialaddernot_9_xyout, Y7);
  xor xor_3 (xor_3_out, multiplier_partialaddernot_10_xyout, Y7);
  xor xor_4 (xor_4_out, multiplier_partialaddernot_11_xyout, Y7);
  xor xor_5 (xor_5_out, multiplier_partialaddernot_12_xyout, Y7);
  xor xor_6 (xor_6_out, multiplier_partialaddernot_13_xyout, Y7);
  xor xor_7 (xor_7_out, multiplier_partialadder_43_xyout, Y7);
  xor xor_8 (xor_8_out, multiplier_partialadder_44_xyout, Y7);
  or or_1 (OVERFLOW, xor_1_out, xor_2_out, xor_3_out, xor_4_out, xor_5_out, xor_6_out, xor_7_out, xor_8_out);

  // Notes on the sheet:
  //   0
  //   1
  //   2
  //   3
  //   4
  //   5
  //   6
  //   7
  //   8
  //   9
  //   10
  //   11
  //   12
  //   13
  //   14
  //   15
endmodule

module ARITHMETIC_Divider (
  input  A0,
  input  A1,
  input  A2,
  input  A3,
  input  A4,
  input  A5,
  input  A6,
  input  A7,
  input  B0,
  input  B1,
  input  B2,
  input  B3,
  input  B4,
  input  B5,
  input  B6,
  input  B7,
  output Y0,
  output Y1,
  output Y2,
  output Y3,
  output Y4,
  output Y5,
  output Y6,
  output Y7,
  output OVERFLOW
);

  wire divider_subtractmultiplexer_1_bout, divider_subtractmultiplexer_2_bout,
       divider_subtractmultiplexer_3_bout, divider_subtractmultiplexer_3_d,
       divider_subtractmultiplexer_4_bout, divider_subtractmultiplexer_4_d,
       divider_subtractmultiplexer_5_bout, divider_subtractmultiplexer_5_d,
       divider_subtractmultiplexer_6_bout, divider_subtractmultiplexer_7_bout,
       divider_subtractmultiplexer_7_d, divider_subtractmultiplexer_8_bout, divider_subtractmultiplexer_8_d,
       divider_subtractmultiplexer_9_bout, divider_subtractmultiplexer_9_d,
       divider_subtractmultiplexer_10_bout, divider_subtractmultiplexer_11_bout,
       divider_subtractmultiplexer_11_d, divider_subtractmultiplexer_12_bout,
       divider_subtractmultiplexer_12_d, divider_subtractmultiplexer_13_bout,
       divider_subtractmultiplexer_13_d, divider_subtractmultiplexer_14_bout,
       divider_subtractmultiplexer_14_d, divider_subtractmultiplexer_15_bout,
       divider_subtractmultiplexer_16_bout, divider_subtractmultiplexer_17_bout,
       divider_subtractmultiplexer_17_d, divider_subtractmultiplexer_18_bout,
       divider_subtractmultiplexer_18_d, divider_subtractmultiplexer_19_bout,
       divider_subtractmultiplexer_19_d, divider_subtractmultiplexer_20_bout,
       divider_subtractmultiplexer_20_d, divider_subtractmultiplexer_21_bout,
       divider_subtractmultiplexer_21_d, divider_subtractmultiplexer_22_bout,
       divider_subtractmultiplexer_22_d, divider_subtractmultiplexer_23_bout,
       divider_subtractmultiplexer_23_d, divider_subtractmultiplexer_24_bout,
       divider_subtractmultiplexer_25_bout, divider_subtractmultiplexer_25_d,
       divider_subtractmultiplexer_26_bout, divider_subtractmultiplexer_26_d,
       divider_subtractmultiplexer_27_bout, divider_subtractmultiplexer_27_d,
       divider_subtractmultiplexer_28_bout, divider_subtractmultiplexer_28_d,
       divider_subtractmultiplexer_29_bout, divider_subtractmultiplexer_29_d,
       divider_subtractmultiplexer_30_bout, divider_subtractmultiplexer_30_d,
       divider_subtractmultiplexer_31_bout, divider_subtractmultiplexer_31_d,
       divider_subtractmultiplexer_32_bout, divider_subtractmultiplexer_32_d,
       divider_subtractmultiplexer_33_bout, divider_subtractmultiplexer_33_d,
       divider_subtractmultiplexer_34_bout, divider_subtractmultiplexer_34_d,
       divider_subtractmultiplexer_35_bout, divider_subtractmultiplexer_35_d,
       divider_subtractmultiplexer_36_bout, divider_subtractmultiplexer_36_d,
       divider_subtractmultiplexer_37_bout, divider_subtractmultiplexer_37_d,
       divider_subtractmultiplexer_38_bout, divider_subtractmultiplexer_38_d,
       divider_subtractmultiplexer_39_bout, divider_subtractmultiplexer_39_d,
       divider_subtractmultiplexer_40_bout, divider_subtractmultiplexer_40_d,
       divider_subtractmultiplexer_41_bout, divider_subtractmultiplexer_41_d,
       divider_subtractmultiplexer_42_bout, divider_subtractmultiplexer_42_d,
       divider_subtractmultiplexer_43_bout, divider_subtractmultiplexer_43_d,
       divider_subtractmultiplexer_44_bout, divider_subtractmultiplexer_44_d,
       divider_subtractmultiplexer_45_bout, divider_subtractmultiplexer_45_d,
       divider_subtractmultiplexer_46_bout, divider_subtractmultiplexer_46_d,
       divider_subtractmultiplexer_47_bout, divider_subtractmultiplexer_47_d,
       divider_subtractmultiplexer_48_bout, divider_subtractmultiplexer_48_d,
       divider_subtractmultiplexer_49_bout, divider_subtractmultiplexer_49_d,
       divider_subtractmultiplexer_50_bout, divider_subtractmultiplexer_50_d,
       divider_subtractmultiplexer_51_bout, divider_subtractmultiplexer_51_d,
       divider_subtractmultiplexer_52_bout, divider_subtractmultiplexer_52_d,
       divider_subtractmultiplexer_53_bout, divider_subtractmultiplexer_53_d,
       divider_subtractmultiplexer_54_bout, divider_subtractmultiplexer_54_d,
       divider_subtractmultiplexer_55_bout, divider_subtractmultiplexer_55_d,
       divider_subtractmultiplexer_56_bout, divider_subtractmultiplexer_56_d,
       divider_subtractmultiplexer_57_bout, divider_subtractmultiplexer_57_d,
       divider_subtractmultiplexer_58_bout, divider_subtractmultiplexer_58_d,
       divider_subtractmultiplexer_59_bout, divider_subtractmultiplexer_59_d,
       divider_subtractmultiplexer_60_bout, divider_subtractmultiplexer_60_d,
       divider_subtractmultiplexer_61_bout, divider_subtractmultiplexer_61_d,
       divider_subtractmultiplexer_62_bout, divider_subtractmultiplexer_62_d,
       divider_subtractmultiplexer_63_bout, divider_subtractmultiplexer_63_d,
       divider_subtractmultiplexer_64_bout, divider_subtractmultiplexer_64_d,
       divider_subtractmultiplexer_65_bout, divider_subtractmultiplexer_65_d,
       divider_subtractmultiplexer_66_bout, divider_subtractmultiplexer_66_d,
       divider_subtractmultiplexer_67_bout, divider_subtractmultiplexer_67_d,
       divider_subtractmultiplexer_68_bout, divider_subtractmultiplexer_68_d,
       divider_subtractmultiplexer_69_bout, divider_subtractmultiplexer_69_d,
       divider_subtractmultiplexer_70_bout, divider_subtractmultiplexer_70_d,
       divider_subtractmultiplexer_71_bout, divider_subtractmultiplexer_71_d,
       divider_subtractmultiplexer_72_bout, divider_subtractmultiplexer_72_d, multiplexer_x2_1_y,
       multiplexer_x2_2_y, multiplexer_x2_3_y, multiplexer_x2_4_y, multiplexer_x2_5_y, multiplexer_x2_6_y,
       multiplexer_x2_7_y, multiplexer_x2_8_y, multiplexer_x2_9_y, multiplexer_x2_10_y, multiplexer_x2_11_y,
       multiplexer_x2_12_y, multiplexer_x2_13_y, multiplexer_x2_14_y, multiplexer_x2_15_y,
       multiplexer_x2_16_y, multiplier_fulladder_1_cout, multiplier_fulladder_1_xyout,
       multiplier_fulladder_2_cout, multiplier_fulladder_2_xyout, multiplier_fulladder_3_cout,
       multiplier_fulladder_3_xyout, multiplier_fulladder_4_cout, multiplier_fulladder_4_xyout,
       multiplier_fulladder_5_cout, multiplier_fulladder_5_xyout, multiplier_fulladder_6_cout,
       multiplier_fulladder_6_xyout, multiplier_fulladder_7_cout, multiplier_fulladder_7_xyout,
       multiplier_fulladder_8_xyout, multiplier_fulladder_9_cout, multiplier_fulladder_9_xyout,
       multiplier_fulladder_10_cout, multiplier_fulladder_10_xyout, multiplier_fulladder_11_cout,
       multiplier_fulladder_11_xyout, multiplier_fulladder_12_cout, multiplier_fulladder_12_xyout,
       multiplier_fulladder_13_cout, multiplier_fulladder_13_xyout, multiplier_fulladder_14_cout,
       multiplier_fulladder_14_xyout, multiplier_fulladder_15_cout, multiplier_fulladder_15_xyout,
       multiplier_fulladder_16_xyout, multiplier_fulladder_17_cout, multiplier_fulladder_17_xyout,
       multiplier_fulladder_18_cout, multiplier_fulladder_18_xyout, multiplier_fulladder_19_cout,
       multiplier_fulladder_19_xyout, multiplier_fulladder_20_cout, multiplier_fulladder_20_xyout,
       multiplier_fulladder_21_cout, multiplier_fulladder_21_xyout, multiplier_fulladder_22_cout,
       multiplier_fulladder_22_xyout, multiplier_fulladder_23_cout, multiplier_fulladder_23_xyout,
       multiplier_fulladder_24_xyout, not_1_out, not_2_out, not_3_out, not_4_out, not_5_out, not_6_out,
       not_7_out, not_8_out, not_9_out, not_10_out, not_11_out, not_12_out, not_13_out, not_14_out,
       not_15_out, not_16_out, not_17_out, not_18_out, not_19_out, not_20_out, not_21_out, not_22_out,
       not_23_out, not_24_out, not_25_out, not_26_out, not_27_out, not_28_out, not_29_out, not_30_out,
       not_31_out, not_32_out, xor_1_out;

  xor xor_1 (xor_1_out, A7, B7);
  not not_1 (not_1_out, A0);
  not not_2 (not_2_out, A1);
  not not_3 (not_3_out, A2);
  not not_4 (not_4_out, A3);
  not not_5 (not_5_out, A4);
  not not_6 (not_6_out, A5);
  not not_7 (not_7_out, A6);
  not not_8 (not_8_out, A7);
  not not_9 (not_9_out, B0);
  not not_10 (not_10_out, B1);
  not not_11 (not_11_out, B2);
  not not_12 (not_12_out, B3);
  not not_13 (not_13_out, B4);
  not not_14 (not_14_out, B5);
  not not_15 (not_15_out, B6);
  not not_16 (not_16_out, B7);
  MULTIPLIER_FullAdder multiplier_fulladder_1 (
    .Xin(not_1_out), .Yin(1'b1), .Cout(multiplier_fulladder_1_cout), .XYout(multiplier_fulladder_1_xyout));  // open: Cin
  MULTIPLIER_FullAdder multiplier_fulladder_2 (
    .Xin(not_2_out), .Yin(1'b0), .Cin(multiplier_fulladder_1_cout), .Cout(multiplier_fulladder_2_cout),
    .XYout(multiplier_fulladder_2_xyout));
  MULTIPLIER_FullAdder multiplier_fulladder_3 (
    .Xin(not_3_out), .Yin(1'b0), .Cin(multiplier_fulladder_2_cout), .Cout(multiplier_fulladder_3_cout),
    .XYout(multiplier_fulladder_3_xyout));
  MULTIPLIER_FullAdder multiplier_fulladder_4 (
    .Xin(not_4_out), .Yin(1'b0), .Cin(multiplier_fulladder_3_cout), .Cout(multiplier_fulladder_4_cout),
    .XYout(multiplier_fulladder_4_xyout));
  MULTIPLIER_FullAdder multiplier_fulladder_5 (
    .Xin(not_5_out), .Yin(1'b0), .Cin(multiplier_fulladder_4_cout), .Cout(multiplier_fulladder_5_cout),
    .XYout(multiplier_fulladder_5_xyout));
  MULTIPLIER_FullAdder multiplier_fulladder_6 (
    .Xin(not_6_out), .Yin(1'b0), .Cin(multiplier_fulladder_5_cout), .Cout(multiplier_fulladder_6_cout),
    .XYout(multiplier_fulladder_6_xyout));
  MULTIPLIER_FullAdder multiplier_fulladder_7 (
    .Xin(not_7_out), .Yin(1'b0), .Cin(multiplier_fulladder_6_cout), .Cout(multiplier_fulladder_7_cout),
    .XYout(multiplier_fulladder_7_xyout));
  MULTIPLIER_FullAdder multiplier_fulladder_8 (
    .Xin(not_8_out), .Yin(1'b0), .Cin(multiplier_fulladder_7_cout), .XYout(multiplier_fulladder_8_xyout));  // open: Cout
  MULTIPLIER_FullAdder multiplier_fulladder_9 (
    .Xin(not_9_out), .Yin(1'b1), .Cout(multiplier_fulladder_9_cout), .XYout(multiplier_fulladder_9_xyout));  // open: Cin
  MULTIPLIER_FullAdder multiplier_fulladder_10 (
    .Xin(not_10_out), .Yin(1'b0), .Cin(multiplier_fulladder_9_cout), .Cout(multiplier_fulladder_10_cout),
    .XYout(multiplier_fulladder_10_xyout));
  MULTIPLIER_FullAdder multiplier_fulladder_11 (
    .Xin(not_11_out), .Yin(1'b0), .Cin(multiplier_fulladder_10_cout), .Cout(multiplier_fulladder_11_cout),
    .XYout(multiplier_fulladder_11_xyout));
  MULTIPLIER_FullAdder multiplier_fulladder_12 (
    .Xin(not_12_out), .Yin(1'b0), .Cin(multiplier_fulladder_11_cout), .Cout(multiplier_fulladder_12_cout),
    .XYout(multiplier_fulladder_12_xyout));
  MULTIPLIER_FullAdder multiplier_fulladder_13 (
    .Xin(not_13_out), .Yin(1'b0), .Cin(multiplier_fulladder_12_cout), .Cout(multiplier_fulladder_13_cout),
    .XYout(multiplier_fulladder_13_xyout));
  MULTIPLIER_FullAdder multiplier_fulladder_14 (
    .Xin(not_14_out), .Yin(1'b0), .Cin(multiplier_fulladder_13_cout), .Cout(multiplier_fulladder_14_cout),
    .XYout(multiplier_fulladder_14_xyout));
  MULTIPLIER_FullAdder multiplier_fulladder_15 (
    .Xin(not_15_out), .Yin(1'b0), .Cin(multiplier_fulladder_14_cout), .Cout(multiplier_fulladder_15_cout),
    .XYout(multiplier_fulladder_15_xyout));
  MULTIPLIER_FullAdder multiplier_fulladder_16 (
    .Xin(not_16_out), .Yin(1'b0), .Cin(multiplier_fulladder_15_cout), .XYout(multiplier_fulladder_16_xyout));  // open: Cout
  not not_17 (not_17_out, divider_subtractmultiplexer_1_bout);
  Multiplexer_x2 multiplexer_x2_1 (.C(A7), .D0(A0), .D1(multiplier_fulladder_1_xyout), .Y(multiplexer_x2_1_y));
  Multiplexer_x2 multiplexer_x2_2 (.C(A7), .D0(A1), .D1(multiplier_fulladder_2_xyout), .Y(multiplexer_x2_2_y));
  Multiplexer_x2 multiplexer_x2_3 (.C(A7), .D0(A2), .D1(multiplier_fulladder_3_xyout), .Y(multiplexer_x2_3_y));
  Multiplexer_x2 multiplexer_x2_4 (.C(A7), .D0(A3), .D1(multiplier_fulladder_4_xyout), .Y(multiplexer_x2_4_y));
  Multiplexer_x2 multiplexer_x2_5 (.C(A7), .D0(A4), .D1(multiplier_fulladder_5_xyout), .Y(multiplexer_x2_5_y));
  Multiplexer_x2 multiplexer_x2_6 (.C(A7), .D0(A5), .D1(multiplier_fulladder_6_xyout), .Y(multiplexer_x2_6_y));
  Multiplexer_x2 multiplexer_x2_7 (.C(A7), .D0(A6), .D1(multiplier_fulladder_7_xyout), .Y(multiplexer_x2_7_y));
  Multiplexer_x2 multiplexer_x2_8 (.C(A7), .D0(A7), .D1(multiplier_fulladder_8_xyout), .Y(multiplexer_x2_8_y));
  Multiplexer_x2 multiplexer_x2_9 (.C(B7), .D0(B0), .D1(multiplier_fulladder_9_xyout), .Y(multiplexer_x2_9_y));
  Multiplexer_x2 multiplexer_x2_10 (.C(B7), .D0(B1), .D1(multiplier_fulladder_10_xyout), .Y(multiplexer_x2_10_y));
  Multiplexer_x2 multiplexer_x2_11 (.C(B7), .D0(B2), .D1(multiplier_fulladder_11_xyout), .Y(multiplexer_x2_11_y));
  Multiplexer_x2 multiplexer_x2_12 (.C(B7), .D0(B3), .D1(multiplier_fulladder_12_xyout), .Y(multiplexer_x2_12_y));
  Multiplexer_x2 multiplexer_x2_13 (.C(B7), .D0(B4), .D1(multiplier_fulladder_13_xyout), .Y(multiplexer_x2_13_y));
  Multiplexer_x2 multiplexer_x2_14 (.C(B7), .D0(B5), .D1(multiplier_fulladder_14_xyout), .Y(multiplexer_x2_14_y));
  Multiplexer_x2 multiplexer_x2_15 (.C(B7), .D0(B6), .D1(multiplier_fulladder_15_xyout), .Y(multiplexer_x2_15_y));
  Multiplexer_x2 multiplexer_x2_16 (.C(B7), .D0(B7), .D1(multiplier_fulladder_16_xyout), .Y(multiplexer_x2_16_y));
  DIVIDER_SubtractMultiplexer divider_subtractmultiplexer_1 (
    .C(divider_subtractmultiplexer_1_bout), .B(1'b0), .A(1'b0), .Bin(divider_subtractmultiplexer_3_bout),
    .Bout(divider_subtractmultiplexer_1_bout));  // open: D
  DIVIDER_SubtractMultiplexer divider_subtractmultiplexer_2 (
    .C(divider_subtractmultiplexer_2_bout), .B(1'b0), .A(divider_subtractmultiplexer_3_d),
    .Bin(divider_subtractmultiplexer_5_bout), .Bout(divider_subtractmultiplexer_2_bout));  // open: D
  not not_18 (not_18_out, divider_subtractmultiplexer_2_bout);
  not not_19 (not_19_out, divider_subtractmultiplexer_6_bout);
  DIVIDER_SubtractMultiplexer divider_subtractmultiplexer_3 (
    .C(divider_subtractmultiplexer_1_bout), .B(multiplexer_x2_16_y), .A(1'b0),
    .Bin(divider_subtractmultiplexer_4_bout), .Bout(divider_subtractmultiplexer_3_bout),
    .D(divider_subtractmultiplexer_3_d));
  DIVIDER_SubtractMultiplexer divider_subtractmultiplexer_4 (
    .C(divider_subtractmultiplexer_1_bout), .B(multiplexer_x2_15_y), .A(1'b0),
    .Bin(divider_subtractmultiplexer_7_bout), .Bout(divider_subtractmultiplexer_4_bout),
    .D(divider_subtractmultiplexer_4_d));
  DIVIDER_SubtractMultiplexer divider_subtractmultiplexer_5 (
    .C(divider_subtractmultiplexer_2_bout), .B(multiplexer_x2_16_y), .A(divider_subtractmultiplexer_4_d),
    .Bin(divider_subtractmultiplexer_8_bout), .Bout(divider_subtractmultiplexer_5_bout),
    .D(divider_subtractmultiplexer_5_d));
  DIVIDER_SubtractMultiplexer divider_subtractmultiplexer_6 (
    .C(divider_subtractmultiplexer_6_bout), .B(1'b0), .A(divider_subtractmultiplexer_5_d),
    .Bin(divider_subtractmultiplexer_9_bout), .Bout(divider_subtractmultiplexer_6_bout));  // open: D
  not not_20 (not_20_out, divider_subtractmultiplexer_10_bout);
  DIVIDER_SubtractMultiplexer divider_subtractmultiplexer_7 (
    .C(divider_subtractmultiplexer_1_bout), .B(multiplexer_x2_14_y), .A(1'b0),
    .Bin(divider_subtractmultiplexer_11_bout), .Bout(divider_subtractmultiplexer_7_bout),
    .D(divider_subtractmultiplexer_7_d));
  DIVIDER_SubtractMultiplexer divider_subtractmultiplexer_8 (
    .C(divider_subtractmultiplexer_2_bout), .B(multiplexer_x2_15_y), .A(divider_subtractmultiplexer_7_d),
    .Bin(divider_subtractmultiplexer_12_bout), .Bout(divider_subtractmultiplexer_8_bout),
    .D(divider_subtractmultiplexer_8_d));
  DIVIDER_SubtractMultiplexer divider_subtractmultiplexer_9 (
    .C(divider_subtractmultiplexer_6_bout), .B(multiplexer_x2_16_y), .A(divider_subtractmultiplexer_8_d),
    .Bin(divider_subtractmultiplexer_13_bout), .Bout(divider_subtractmultiplexer_9_bout),
    .D(divider_subtractmultiplexer_9_d));
  DIVIDER_SubtractMultiplexer divider_subtractmultiplexer_10 (
    .C(divider_subtractmultiplexer_10_bout), .B(1'b0), .A(divider_subtractmultiplexer_9_d),
    .Bin(divider_subtractmultiplexer_14_bout), .Bout(divider_subtractmultiplexer_10_bout));  // open: D
  not not_21 (not_21_out, divider_subtractmultiplexer_15_bout);
  DIVIDER_SubtractMultiplexer divider_subtractmultiplexer_11 (
    .C(divider_subtractmultiplexer_1_bout), .B(multiplexer_x2_13_y), .A(1'b0),
    .Bin(divider_subtractmultiplexer_17_bout), .Bout(divider_subtractmultiplexer_11_bout),
    .D(divider_subtractmultiplexer_11_d));
  DIVIDER_SubtractMultiplexer divider_subtractmultiplexer_12 (
    .C(divider_subtractmultiplexer_2_bout), .B(multiplexer_x2_14_y), .A(divider_subtractmultiplexer_11_d),
    .Bin(divider_subtractmultiplexer_18_bout), .Bout(divider_subtractmultiplexer_12_bout),
    .D(divider_subtractmultiplexer_12_d));
  DIVIDER_SubtractMultiplexer divider_subtractmultiplexer_13 (
    .C(divider_subtractmultiplexer_6_bout), .B(multiplexer_x2_15_y), .A(divider_subtractmultiplexer_12_d),
    .Bin(divider_subtractmultiplexer_19_bout), .Bout(divider_subtractmultiplexer_13_bout),
    .D(divider_subtractmultiplexer_13_d));
  DIVIDER_SubtractMultiplexer divider_subtractmultiplexer_14 (
    .C(divider_subtractmultiplexer_10_bout), .B(multiplexer_x2_16_y), .A(divider_subtractmultiplexer_13_d),
    .Bin(divider_subtractmultiplexer_20_bout), .Bout(divider_subtractmultiplexer_14_bout),
    .D(divider_subtractmultiplexer_14_d));
  DIVIDER_SubtractMultiplexer divider_subtractmultiplexer_15 (
    .C(divider_subtractmultiplexer_15_bout), .B(1'b0), .A(divider_subtractmultiplexer_14_d),
    .Bin(divider_subtractmultiplexer_21_bout), .Bout(divider_subtractmultiplexer_15_bout));  // open: D
  DIVIDER_SubtractMultiplexer divider_subtractmultiplexer_16 (
    .C(divider_subtractmultiplexer_16_bout), .B(1'b0), .A(divider_subtractmultiplexer_21_d),
    .Bin(divider_subtractmultiplexer_23_bout), .Bout(divider_subtractmultiplexer_16_bout));  // open: D
  not not_22 (not_22_out, divider_subtractmultiplexer_16_bout);
  not not_23 (not_23_out, divider_subtractmultiplexer_24_bout);
  DIVIDER_SubtractMultiplexer divider_subtractmultiplexer_17 (
    .C(divider_subtractmultiplexer_1_bout), .B(multiplexer_x2_12_y), .A(1'b0),
    .Bin(divider_subtractmultiplexer_25_bout), .Bout(divider_subtractmultiplexer_17_bout),
    .D(divider_subtractmultiplexer_17_d));
  DIVIDER_SubtractMultiplexer divider_subtractmultiplexer_18 (
    .C(divider_subtractmultiplexer_2_bout), .B(multiplexer_x2_13_y), .A(divider_subtractmultiplexer_17_d),
    .Bin(divider_subtractmultiplexer_26_bout), .Bout(divider_subtractmultiplexer_18_bout),
    .D(divider_subtractmultiplexer_18_d));
  DIVIDER_SubtractMultiplexer divider_subtractmultiplexer_19 (
    .C(divider_subtractmultiplexer_6_bout), .B(multiplexer_x2_14_y), .A(divider_subtractmultiplexer_18_d),
    .Bin(divider_subtractmultiplexer_27_bout), .Bout(divider_subtractmultiplexer_19_bout),
    .D(divider_subtractmultiplexer_19_d));
  DIVIDER_SubtractMultiplexer divider_subtractmultiplexer_20 (
    .C(divider_subtractmultiplexer_10_bout), .B(multiplexer_x2_15_y), .A(divider_subtractmultiplexer_19_d),
    .Bin(divider_subtractmultiplexer_28_bout), .Bout(divider_subtractmultiplexer_20_bout),
    .D(divider_subtractmultiplexer_20_d));
  DIVIDER_SubtractMultiplexer divider_subtractmultiplexer_21 (
    .C(divider_subtractmultiplexer_15_bout), .B(multiplexer_x2_16_y), .A(divider_subtractmultiplexer_20_d),
    .Bin(divider_subtractmultiplexer_22_bout), .Bout(divider_subtractmultiplexer_21_bout),
    .D(divider_subtractmultiplexer_21_d));
  DIVIDER_SubtractMultiplexer divider_subtractmultiplexer_22 (
    .C(divider_subtractmultiplexer_15_bout), .B(multiplexer_x2_15_y), .A(divider_subtractmultiplexer_28_d),
    .Bin(divider_subtractmultiplexer_30_bout), .Bout(divider_subtractmultiplexer_22_bout),
    .D(divider_subtractmultiplexer_22_d));
  DIVIDER_SubtractMultiplexer divider_subtractmultiplexer_23 (
    .C(divider_subtractmultiplexer_16_bout), .B(multiplexer_x2_16_y), .A(divider_subtractmultiplexer_22_d),
    .Bin(divider_subtractmultiplexer_31_bout), .Bout(divider_subtractmultiplexer_23_bout),
    .D(divider_subtractmultiplexer_23_d));
  DIVIDER_SubtractMultiplexer divider_subtractmultiplexer_24 (
    .C(divider_subtractmultiplexer_24_bout), .B(1'b0), .A(divider_subtractmultiplexer_23_d),
    .Bin(divider_subtractmultiplexer_32_bout), .Bout(divider_subtractmultiplexer_24_bout));  // open: D
  not not_24 (not_24_out, divider_subtractmultiplexer_33_bout);
  DIVIDER_SubtractMultiplexer divider_subtractmultiplexer_25 (
    .C(divider_subtractmultiplexer_1_bout), .B(multiplexer_x2_11_y), .A(1'b0),
    .Bin(divider_subtractmultiplexer_34_bout), .Bout(divider_subtractmultiplexer_25_bout),
    .D(divider_subtractmultiplexer_25_d));
  DIVIDER_SubtractMultiplexer divider_subtractmultiplexer_26 (
    .C(divider_subtractmultiplexer_2_bout), .B(multiplexer_x2_12_y), .A(divider_subtractmultiplexer_25_d),
    .Bin(divider_subtractmultiplexer_35_bout), .Bout(divider_subtractmultiplexer_26_bout),
    .D(divider_subtractmultiplexer_26_d));
  DIVIDER_SubtractMultiplexer divider_subtractmultiplexer_27 (
    .C(divider_subtractmultiplexer_6_bout), .B(multiplexer_x2_13_y), .A(divider_subtractmultiplexer_26_d),
    .Bin(divider_subtractmultiplexer_36_bout), .Bout(divider_subtractmultiplexer_27_bout),
    .D(divider_subtractmultiplexer_27_d));
  DIVIDER_SubtractMultiplexer divider_subtractmultiplexer_28 (
    .C(divider_subtractmultiplexer_10_bout), .B(multiplexer_x2_14_y), .A(divider_subtractmultiplexer_27_d),
    .Bin(divider_subtractmultiplexer_29_bout), .Bout(divider_subtractmultiplexer_28_bout),
    .D(divider_subtractmultiplexer_28_d));
  DIVIDER_SubtractMultiplexer divider_subtractmultiplexer_29 (
    .C(divider_subtractmultiplexer_10_bout), .B(multiplexer_x2_13_y), .A(divider_subtractmultiplexer_36_d),
    .Bin(divider_subtractmultiplexer_38_bout), .Bout(divider_subtractmultiplexer_29_bout),
    .D(divider_subtractmultiplexer_29_d));
  DIVIDER_SubtractMultiplexer divider_subtractmultiplexer_30 (
    .C(divider_subtractmultiplexer_15_bout), .B(multiplexer_x2_14_y), .A(divider_subtractmultiplexer_29_d),
    .Bin(divider_subtractmultiplexer_39_bout), .Bout(divider_subtractmultiplexer_30_bout),
    .D(divider_subtractmultiplexer_30_d));
  DIVIDER_SubtractMultiplexer divider_subtractmultiplexer_31 (
    .C(divider_subtractmultiplexer_16_bout), .B(multiplexer_x2_15_y), .A(divider_subtractmultiplexer_30_d),
    .Bin(divider_subtractmultiplexer_40_bout), .Bout(divider_subtractmultiplexer_31_bout),
    .D(divider_subtractmultiplexer_31_d));
  DIVIDER_SubtractMultiplexer divider_subtractmultiplexer_32 (
    .C(divider_subtractmultiplexer_24_bout), .B(multiplexer_x2_16_y), .A(divider_subtractmultiplexer_31_d),
    .Bin(divider_subtractmultiplexer_41_bout), .Bout(divider_subtractmultiplexer_32_bout),
    .D(divider_subtractmultiplexer_32_d));
  DIVIDER_SubtractMultiplexer divider_subtractmultiplexer_33 (
    .C(divider_subtractmultiplexer_33_bout), .B(1'b0), .A(divider_subtractmultiplexer_32_d),
    .Bin(divider_subtractmultiplexer_42_bout), .Bout(divider_subtractmultiplexer_33_bout),
    .D(divider_subtractmultiplexer_33_d));
  not not_25 (not_25_out, not_24_out);
  not not_26 (not_26_out, not_23_out);
  not not_27 (not_27_out, not_22_out);
  not not_28 (not_28_out, not_21_out);
  not not_29 (not_29_out, not_20_out);
  not not_30 (not_30_out, not_19_out);
  not not_31 (not_31_out, not_18_out);
  not not_32 (not_32_out, not_17_out);
  DIVIDER_SubtractMultiplexer divider_subtractmultiplexer_34 (
    .C(divider_subtractmultiplexer_1_bout), .B(multiplexer_x2_10_y), .A(1'b0),
    .Bin(divider_subtractmultiplexer_43_bout), .Bout(divider_subtractmultiplexer_34_bout),
    .D(divider_subtractmultiplexer_34_d));
  DIVIDER_SubtractMultiplexer divider_subtractmultiplexer_35 (
    .C(divider_subtractmultiplexer_2_bout), .B(multiplexer_x2_11_y), .A(divider_subtractmultiplexer_34_d),
    .Bin(divider_subtractmultiplexer_44_bout), .Bout(divider_subtractmultiplexer_35_bout),
    .D(divider_subtractmultiplexer_35_d));
  DIVIDER_SubtractMultiplexer divider_subtractmultiplexer_36 (
    .C(divider_subtractmultiplexer_6_bout), .B(multiplexer_x2_12_y), .A(divider_subtractmultiplexer_35_d),
    .Bin(divider_subtractmultiplexer_37_bout), .Bout(divider_subtractmultiplexer_36_bout),
    .D(divider_subtractmultiplexer_36_d));
  DIVIDER_SubtractMultiplexer divider_subtractmultiplexer_37 (
    .C(divider_subtractmultiplexer_6_bout), .B(multiplexer_x2_11_y), .A(divider_subtractmultiplexer_44_d),
    .Bin(divider_subtractmultiplexer_46_bout), .Bout(divider_subtractmultiplexer_37_bout),
    .D(divider_subtractmultiplexer_37_d));
  DIVIDER_SubtractMultiplexer divider_subtractmultiplexer_38 (
    .C(divider_subtractmultiplexer_10_bout), .B(multiplexer_x2_12_y), .A(divider_subtractmultiplexer_37_d),
    .Bin(divider_subtractmultiplexer_47_bout), .Bout(divider_subtractmultiplexer_38_bout),
    .D(divider_subtractmultiplexer_38_d));
  DIVIDER_SubtractMultiplexer divider_subtractmultiplexer_39 (
    .C(divider_subtractmultiplexer_15_bout), .B(multiplexer_x2_13_y), .A(divider_subtractmultiplexer_38_d),
    .Bin(divider_subtractmultiplexer_48_bout), .Bout(divider_subtractmultiplexer_39_bout),
    .D(divider_subtractmultiplexer_39_d));
  DIVIDER_SubtractMultiplexer divider_subtractmultiplexer_40 (
    .C(divider_subtractmultiplexer_16_bout), .B(multiplexer_x2_14_y), .A(divider_subtractmultiplexer_39_d),
    .Bin(divider_subtractmultiplexer_49_bout), .Bout(divider_subtractmultiplexer_40_bout),
    .D(divider_subtractmultiplexer_40_d));
  DIVIDER_SubtractMultiplexer divider_subtractmultiplexer_41 (
    .C(divider_subtractmultiplexer_24_bout), .B(multiplexer_x2_15_y), .A(divider_subtractmultiplexer_40_d),
    .Bin(divider_subtractmultiplexer_50_bout), .Bout(divider_subtractmultiplexer_41_bout),
    .D(divider_subtractmultiplexer_41_d));
  DIVIDER_SubtractMultiplexer divider_subtractmultiplexer_42 (
    .C(divider_subtractmultiplexer_33_bout), .B(multiplexer_x2_16_y), .A(divider_subtractmultiplexer_41_d),
    .Bin(divider_subtractmultiplexer_51_bout), .Bout(divider_subtractmultiplexer_42_bout),
    .D(divider_subtractmultiplexer_42_d));
  DIVIDER_SubtractMultiplexer divider_subtractmultiplexer_43 (
    .C(divider_subtractmultiplexer_1_bout), .B(multiplexer_x2_9_y), .A(multiplexer_x2_8_y), .Bin(1'b0),
    .Bout(divider_subtractmultiplexer_43_bout), .D(divider_subtractmultiplexer_43_d));
  DIVIDER_SubtractMultiplexer divider_subtractmultiplexer_44 (
    .C(divider_subtractmultiplexer_2_bout), .B(multiplexer_x2_10_y), .A(divider_subtractmultiplexer_43_d),
    .Bin(divider_subtractmultiplexer_45_bout), .Bout(divider_subtractmultiplexer_44_bout),
    .D(divider_subtractmultiplexer_44_d));
  DIVIDER_SubtractMultiplexer divider_subtractmultiplexer_45 (
    .C(divider_subtractmultiplexer_2_bout), .B(multiplexer_x2_9_y), .A(multiplexer_x2_7_y), .Bin(1'b0),
    .Bout(divider_subtractmultiplexer_45_bout), .D(divider_subtractmultiplexer_45_d));
  DIVIDER_SubtractMultiplexer divider_subtractmultiplexer_46 (
    .C(divider_subtractmultiplexer_6_bout), .B(multiplexer_x2_10_y), .A(divider_subtractmultiplexer_45_d),
    .Bin(divider_subtractmultiplexer_52_bout), .Bout(divider_subtractmultiplexer_46_bout),
    .D(divider_subtractmultiplexer_46_d));
  DIVIDER_SubtractMultiplexer divider_subtractmultiplexer_47 (
    .C(divider_subtractmultiplexer_10_bout), .B(multiplexer_x2_11_y), .A(divider_subtractmultiplexer_46_d),
    .Bin(divider_subtractmultiplexer_53_bout), .Bout(divider_subtractmultiplexer_47_bout),
    .D(divider_subtractmultiplexer_47_d));
  DIVIDER_SubtractMultiplexer divider_subtractmultiplexer_48 (
    .C(divider_subtractmultiplexer_15_bout), .B(multiplexer_x2_12_y), .A(divider_subtractmultiplexer_47_d),
    .Bin(divider_subtractmultiplexer_54_bout), .Bout(divider_subtractmultiplexer_48_bout),
    .D(divider_subtractmultiplexer_48_d));
  DIVIDER_SubtractMultiplexer divider_subtractmultiplexer_49 (
    .C(divider_subtractmultiplexer_16_bout), .B(multiplexer_x2_13_y), .A(divider_subtractmultiplexer_48_d),
    .Bin(divider_subtractmultiplexer_55_bout), .Bout(divider_subtractmultiplexer_49_bout),
    .D(divider_subtractmultiplexer_49_d));
  DIVIDER_SubtractMultiplexer divider_subtractmultiplexer_50 (
    .C(divider_subtractmultiplexer_24_bout), .B(multiplexer_x2_14_y), .A(divider_subtractmultiplexer_49_d),
    .Bin(divider_subtractmultiplexer_56_bout), .Bout(divider_subtractmultiplexer_50_bout),
    .D(divider_subtractmultiplexer_50_d));
  DIVIDER_SubtractMultiplexer divider_subtractmultiplexer_51 (
    .C(divider_subtractmultiplexer_33_bout), .B(multiplexer_x2_15_y), .A(divider_subtractmultiplexer_50_d),
    .Bin(divider_subtractmultiplexer_57_bout), .Bout(divider_subtractmultiplexer_51_bout),
    .D(divider_subtractmultiplexer_51_d));
  MULTIPLIER_FullAdder multiplier_fulladder_17 (
    .Xin(not_25_out), .Yin(1'b1), .Cout(multiplier_fulladder_17_cout), .XYout(multiplier_fulladder_17_xyout));  // open: Cin
  MULTIPLIER_FullAdder multiplier_fulladder_18 (
    .Xin(not_26_out), .Yin(1'b0), .Cin(multiplier_fulladder_17_cout), .Cout(multiplier_fulladder_18_cout),
    .XYout(multiplier_fulladder_18_xyout));
  MULTIPLIER_FullAdder multiplier_fulladder_19 (
    .Xin(not_27_out), .Yin(1'b0), .Cin(multiplier_fulladder_18_cout), .Cout(multiplier_fulladder_19_cout),
    .XYout(multiplier_fulladder_19_xyout));
  MULTIPLIER_FullAdder multiplier_fulladder_20 (
    .Xin(not_28_out), .Yin(1'b0), .Cin(multiplier_fulladder_19_cout), .Cout(multiplier_fulladder_20_cout),
    .XYout(multiplier_fulladder_20_xyout));
  MULTIPLIER_FullAdder multiplier_fulladder_21 (
    .Xin(not_29_out), .Yin(1'b0), .Cin(multiplier_fulladder_20_cout), .Cout(multiplier_fulladder_21_cout),
    .XYout(multiplier_fulladder_21_xyout));
  MULTIPLIER_FullAdder multiplier_fulladder_22 (
    .Xin(not_30_out), .Yin(1'b0), .Cin(multiplier_fulladder_21_cout), .Cout(multiplier_fulladder_22_cout),
    .XYout(multiplier_fulladder_22_xyout));
  MULTIPLIER_FullAdder multiplier_fulladder_23 (
    .Xin(not_31_out), .Yin(1'b0), .Cin(multiplier_fulladder_22_cout), .Cout(multiplier_fulladder_23_cout),
    .XYout(multiplier_fulladder_23_xyout));
  MULTIPLIER_FullAdder multiplier_fulladder_24 (
    .Xin(not_32_out), .Yin(1'b0), .Cin(multiplier_fulladder_23_cout), .XYout(multiplier_fulladder_24_xyout));  // open: Cout
  DIVIDER_SubtractMultiplexer divider_subtractmultiplexer_52 (
    .C(divider_subtractmultiplexer_6_bout), .B(multiplexer_x2_9_y), .A(multiplexer_x2_6_y), .Bin(1'b0),
    .Bout(divider_subtractmultiplexer_52_bout), .D(divider_subtractmultiplexer_52_d));
  DIVIDER_SubtractMultiplexer divider_subtractmultiplexer_53 (
    .C(divider_subtractmultiplexer_10_bout), .B(multiplexer_x2_10_y), .A(divider_subtractmultiplexer_52_d),
    .Bin(divider_subtractmultiplexer_59_bout), .Bout(divider_subtractmultiplexer_53_bout),
    .D(divider_subtractmultiplexer_53_d));
  DIVIDER_SubtractMultiplexer divider_subtractmultiplexer_54 (
    .C(divider_subtractmultiplexer_15_bout), .B(multiplexer_x2_11_y), .A(divider_subtractmultiplexer_53_d),
    .Bin(divider_subtractmultiplexer_60_bout), .Bout(divider_subtractmultiplexer_54_bout),
    .D(divider_subtractmultiplexer_54_d));
  DIVIDER_SubtractMultiplexer divider_subtractmultiplexer_55 (
    .C(divider_subtractmultiplexer_16_bout), .B(multiplexer_x2_12_y), .A(divider_subtractmultiplexer_54_d),
    .Bin(divider_subtractmultiplexer_61_bout), .Bout(divider_subtractmultiplexer_55_bout),
    .D(divider_subtractmultiplexer_55_d));
  DIVIDER_SubtractMultiplexer divider_subtractmultiplexer_56 (
    .C(divider_subtractmultiplexer_24_bout), .B(multiplexer_x2_13_y), .A(divider_subtractmultiplexer_55_d),
    .Bin(divider_subtractmultiplexer_62_bout), .Bout(divider_subtractmultiplexer_56_bout),
    .D(divider_subtractmultiplexer_56_d));
  DIVIDER_SubtractMultiplexer divider_subtractmultiplexer_57 (
    .C(divider_subtractmultiplexer_33_bout), .B(multiplexer_x2_14_y), .A(divider_subtractmultiplexer_56_d),
    .Bin(divider_subtractmultiplexer_58_bout), .Bout(divider_subtractmultiplexer_57_bout),
    .D(divider_subtractmultiplexer_57_d));
  DIVIDER_SubtractMultiplexer divider_subtractmultiplexer_58 (
    .C(divider_subtractmultiplexer_33_bout), .B(multiplexer_x2_13_y), .A(divider_subtractmultiplexer_62_d),
    .Bin(divider_subtractmultiplexer_64_bout), .Bout(divider_subtractmultiplexer_58_bout),
    .D(divider_subtractmultiplexer_58_d));
  or or_1 (OVERFLOW, divider_subtractmultiplexer_33_d, divider_subtractmultiplexer_42_d, divider_subtractmultiplexer_51_d, divider_subtractmultiplexer_57_d, divider_subtractmultiplexer_58_d, divider_subtractmultiplexer_64_d, divider_subtractmultiplexer_69_d, divider_subtractmultiplexer_71_d, divider_subtractmultiplexer_72_d);
  DIVIDER_SubtractMultiplexer divider_subtractmultiplexer_59 (
    .C(divider_subtractmultiplexer_10_bout), .B(multiplexer_x2_9_y), .A(multiplexer_x2_5_y), .Bin(1'b0),
    .Bout(divider_subtractmultiplexer_59_bout), .D(divider_subtractmultiplexer_59_d));
  DIVIDER_SubtractMultiplexer divider_subtractmultiplexer_60 (
    .C(divider_subtractmultiplexer_15_bout), .B(multiplexer_x2_10_y), .A(divider_subtractmultiplexer_59_d),
    .Bin(divider_subtractmultiplexer_65_bout), .Bout(divider_subtractmultiplexer_60_bout),
    .D(divider_subtractmultiplexer_60_d));
  DIVIDER_SubtractMultiplexer divider_subtractmultiplexer_61 (
    .C(divider_subtractmultiplexer_16_bout), .B(multiplexer_x2_11_y), .A(divider_subtractmultiplexer_60_d),
    .Bin(divider_subtractmultiplexer_66_bout), .Bout(divider_subtractmultiplexer_61_bout),
    .D(divider_subtractmultiplexer_61_d));
  DIVIDER_SubtractMultiplexer divider_subtractmultiplexer_62 (
    .C(divider_subtractmultiplexer_24_bout), .B(multiplexer_x2_12_y), .A(divider_subtractmultiplexer_61_d),
    .Bin(divider_subtractmultiplexer_63_bout), .Bout(divider_subtractmultiplexer_62_bout),
    .D(divider_subtractmultiplexer_62_d));
  DIVIDER_SubtractMultiplexer divider_subtractmultiplexer_63 (
    .C(divider_subtractmultiplexer_24_bout), .B(multiplexer_x2_11_y), .A(divider_subtractmultiplexer_66_d),
    .Bin(divider_subtractmultiplexer_68_bout), .Bout(divider_subtractmultiplexer_63_bout),
    .D(divider_subtractmultiplexer_63_d));
  DIVIDER_SubtractMultiplexer divider_subtractmultiplexer_64 (
    .C(divider_subtractmultiplexer_33_bout), .B(multiplexer_x2_12_y), .A(divider_subtractmultiplexer_63_d),
    .Bin(divider_subtractmultiplexer_69_bout), .Bout(divider_subtractmultiplexer_64_bout),
    .D(divider_subtractmultiplexer_64_d));
  DIVIDER_SubtractMultiplexer divider_subtractmultiplexer_65 (
    .C(divider_subtractmultiplexer_15_bout), .B(multiplexer_x2_9_y), .A(multiplexer_x2_4_y), .Bin(1'b0),
    .Bout(divider_subtractmultiplexer_65_bout), .D(divider_subtractmultiplexer_65_d));
  DIVIDER_SubtractMultiplexer divider_subtractmultiplexer_66 (
    .C(divider_subtractmultiplexer_16_bout), .B(multiplexer_x2_10_y), .A(divider_subtractmultiplexer_65_d),
    .Bin(divider_subtractmultiplexer_67_bout), .Bout(divider_subtractmultiplexer_66_bout),
    .D(divider_subtractmultiplexer_66_d));
  DIVIDER_SubtractMultiplexer divider_subtractmultiplexer_67 (
    .C(divider_subtractmultiplexer_16_bout), .B(multiplexer_x2_9_y), .A(multiplexer_x2_3_y), .Bin(1'b0),
    .Bout(divider_subtractmultiplexer_67_bout), .D(divider_subtractmultiplexer_67_d));
  DIVIDER_SubtractMultiplexer divider_subtractmultiplexer_68 (
    .C(divider_subtractmultiplexer_24_bout), .B(multiplexer_x2_10_y), .A(divider_subtractmultiplexer_67_d),
    .Bin(divider_subtractmultiplexer_70_bout), .Bout(divider_subtractmultiplexer_68_bout),
    .D(divider_subtractmultiplexer_68_d));
  DIVIDER_SubtractMultiplexer divider_subtractmultiplexer_69 (
    .C(divider_subtractmultiplexer_33_bout), .B(multiplexer_x2_11_y), .A(divider_subtractmultiplexer_68_d),
    .Bin(divider_subtractmultiplexer_71_bout), .Bout(divider_subtractmultiplexer_69_bout),
    .D(divider_subtractmultiplexer_69_d));
  Multiplexer_x2 multiplexer_x2_17 (.C(xor_1_out), .D0(not_24_out), .D1(multiplier_fulladder_17_xyout), .Y(Y0));
  Multiplexer_x2 multiplexer_x2_18 (.C(xor_1_out), .D0(not_23_out), .D1(multiplier_fulladder_18_xyout), .Y(Y1));
  Multiplexer_x2 multiplexer_x2_19 (.C(xor_1_out), .D0(not_22_out), .D1(multiplier_fulladder_19_xyout), .Y(Y2));
  Multiplexer_x2 multiplexer_x2_20 (.C(xor_1_out), .D0(not_21_out), .D1(multiplier_fulladder_20_xyout), .Y(Y3));
  Multiplexer_x2 multiplexer_x2_21 (.C(xor_1_out), .D0(not_20_out), .D1(multiplier_fulladder_21_xyout), .Y(Y4));
  Multiplexer_x2 multiplexer_x2_22 (.C(xor_1_out), .D0(not_19_out), .D1(multiplier_fulladder_22_xyout), .Y(Y5));
  Multiplexer_x2 multiplexer_x2_23 (.C(xor_1_out), .D0(not_18_out), .D1(multiplier_fulladder_23_xyout), .Y(Y6));
  Multiplexer_x2 multiplexer_x2_24 (.C(xor_1_out), .D0(not_17_out), .D1(multiplier_fulladder_24_xyout), .Y(Y7));
  DIVIDER_SubtractMultiplexer divider_subtractmultiplexer_70 (
    .C(divider_subtractmultiplexer_24_bout), .B(multiplexer_x2_9_y), .A(multiplexer_x2_2_y), .Bin(1'b0),
    .Bout(divider_subtractmultiplexer_70_bout), .D(divider_subtractmultiplexer_70_d));
  DIVIDER_SubtractMultiplexer divider_subtractmultiplexer_71 (
    .C(divider_subtractmultiplexer_33_bout), .B(multiplexer_x2_10_y), .A(divider_subtractmultiplexer_70_d),
    .Bin(divider_subtractmultiplexer_72_bout), .Bout(divider_subtractmultiplexer_71_bout),
    .D(divider_subtractmultiplexer_71_d));
  DIVIDER_SubtractMultiplexer divider_subtractmultiplexer_72 (
    .C(divider_subtractmultiplexer_33_bout), .B(multiplexer_x2_9_y), .A(multiplexer_x2_1_y), .Bin(1'b0),
    .Bout(divider_subtractmultiplexer_72_bout), .D(divider_subtractmultiplexer_72_d));
endmodule

module Multiplexer_x2 (
  input  C,
  input  D0,
  input  D1,
  output Y
);

  wire and_1_out, and_2_out, not_1_out;

  not not_1 (not_1_out, C);
  and and_1 (and_1_out, not_1_out, D0);
  and and_2 (and_2_out, C, D1);
  or or_1 (Y, and_1_out, and_2_out);
endmodule

module Multiplexer_x4 (
  input  C0,
  input  C1,
  input  D0,
  input  D1,
  input  D2,
  input  D3,
  output Y
);

  wire and_1_out, and_2_out, and_3_out, and_4_out, not_1_out, not_2_out, not_3_out, not_4_out;

  not not_1 (not_1_out, C0);
  not not_2 (not_2_out, C1);
  not not_3 (not_3_out, C0);
  not not_4 (not_4_out, C1);
  and and_1 (and_1_out, not_1_out, not_2_out, D0);
  and and_2 (and_2_out, not_3_out, C1, D1);
  and and_3 (and_3_out, C0, not_4_out, D2);
  and and_4 (and_4_out, C0, C1, D3);
  or or_1 (Y, and_1_out, and_2_out, and_3_out, and_4_out);
endmodule

module MULTIPLIER_FullAdder (
  input  Cin,
  input  Xin,
  input  Yin,
  output XYout,
  output Cout
);

  wire and_1_out, and_2_out, xor_1_out;

  and and_1 (and_1_out, Xin, Yin);
  xor xor_1 (xor_1_out, Xin, Yin);
  and and_2 (and_2_out, Cin, xor_1_out);
  or or_1 (Cout, and_1_out, and_2_out);
  xor xor_2 (XYout, Cin, xor_1_out);
endmodule

module MULTIPLIER_PartialAdderNot (
  input  Yin,
  input  Cin,
  input  Xin,
  input  Z,
  output XYout,
  output Xout,
  output Yout,
  output Cout
);

  wire nand_1_out;

  nand nand_1 (nand_1_out, Yin, Xin);
  MULTIPLIER_FullAdder multiplier_fulladder_1 (.Xin(nand_1_out), .Yin(Z), .Cin(Cin), .Cout(Cout), .XYout(XYout));

  assign Xout = Xin;
  assign Yout = Yin;
endmodule

module MULTIPLIER_PartialAdder (
  input  Yin,
  input  Cin,
  input  Xin,
  input  Z,
  output XYout,
  output Xout,
  output Yout,
  output Cout
);

  wire and_1_out;

  and and_1 (and_1_out, Yin, Xin);
  MULTIPLIER_FullAdder multiplier_fulladder_1 (.Xin(and_1_out), .Yin(Z), .Cin(Cin), .Cout(Cout), .XYout(XYout));

  assign Xout = Xin;
  assign Yout = Yin;
endmodule

module DIVIDER_FullSubtractor (
  input  A,
  input  B,
  input  Bin,
  output D,
  output Bout
);

  wire and_1_out, and_2_out, not_1_out, not_2_out, xor_1_out;

  xor xor_1 (xor_1_out, A, B);
  not not_1 (not_1_out, xor_1_out);
  not not_2 (not_2_out, A);
  xor xor_2 (D, xor_1_out, Bin);
  and and_1 (and_1_out, not_1_out, Bin);
  and and_2 (and_2_out, not_2_out, B);
  or or_1 (Bout, and_1_out, and_2_out);
endmodule

module DIVIDER_SubtractMultiplexer (
  input  B,
  input  A,
  input  Bin,
  input  C,
  output Bout,
  output D
);

  wire and_1_out, and_2_out, divider_fullsubtractor_1_d, not_1_out;

  DIVIDER_FullSubtractor divider_fullsubtractor_1 (
    .A(A), .B(B), .Bin(Bin), .D(divider_fullsubtractor_1_d), .Bout(Bout));
  and and_1 (and_1_out, divider_fullsubtractor_1_d, not_1_out);
  not not_1 (not_1_out, C);
  and and_2 (and_2_out, A, C);
  or or_1 (D, and_1_out, and_2_out);
endmodule
