// Logisim project LogisimALU.circ as structural Verilog: 12 circuits, main circuit ALU
module ALU (
  input  CLOCK,
  input  A0,
  input  A1,
  input  A2,
  input  A3,
  input  A4,
  input  A5,
  input  A6,
  input  A7,
  input  B0,
  input  B1,
  input  B2,
  input  B3,
  input  B4,
  input  B5,
  input  B6,
  input  B7,
  input  S0,
  input  S1,
  input  S2,
  input  SUB,
  output Z0,
  output Z1,
  output Z2,
  output Z3,
  output Z4,
  output Z5,
  output Z6,
  output Z7,
  output COUT
);

  wire alu_arithmetic_1_z0, alu_arithmetic_1_z1, alu_arithmetic_1_z2, alu_arithmetic_1_z3,
       alu_arithmetic_1_z4, alu_arithmetic_1_z5, alu_arithmetic_1_z6, alu_arithmetic_1_z7, alu_logic_1_z0,
       alu_logic_1_z1, alu_logic_1_z2, alu_logic_1_z3, alu_logic_1_z4, alu_logic_1_z5, alu_logic_1_z6,
       alu_logic_1_z7, alu_multiplexerx2_1_z, alu_multiplexerx2_2_z, alu_multiplexerx2_3_z,
       alu_multiplexerx2_4_z, alu_multiplexerx2_5_z, alu_multiplexerx2_6_z, alu_multiplexerx2_7_z,
       alu_multiplexerx2_8_z;

  ALU_Logic alu_logic_1 (
    .A0(A0), .A1(A1), .A2(A2), .A3(A3), .A4(A4), .A5(A5), .A6(A6), .A7(A7), .B0(B0), .B1(B1), .B2(B2),
    .B3(B3), .B4(B4), .B5(B5), .B6(B6), .B7(B7), .S0(S0), .S1(S1), .Z0(alu_logic_1_z0), .Z1(alu_logic_1_z1),
    .Z2(alu_logic_1_z2), .Z3(alu_logic_1_z3), .Z4(alu_logic_1_z4), .Z5(alu_logic_1_z5), .Z6(alu_logic_1_z6),
    .Z7(alu_logic_1_z7));
  ALU_Arithmetic alu_arithmetic_1 (
    .A0(A0), .A1(A1), .A2(A2), .A3(A3), .A4(A4), .A5(A5), .A6(A6), .A7(A7), .B0(B0), .B1(B1), .B2(B2),
    .B3(B3), .B4(B4), .B5(B5), .B6(B6), .B7(B7), .SUB(S0), .S0(S1), .S1(SUB), .Z0(alu_arithmetic_1_z0),
    .Z1(alu_arithmetic_1_z1), .Z2(alu_arithmetic_1_z2), .Z3(alu_arithmetic_1_z3), .Z4(alu_arithmetic_1_z4),
    .Z5(alu_arithmetic_1_z5), .Z6(alu_arithmetic_1_z6), .Z7(alu_arithmetic_1_z7), .COUT(COUT));
  ALU_MultiplexerX2 alu_multiplexerx2_1 (
    .S3(S2), .D0(alu_logic_1_z0), .D1(alu_arithmetic_1_z0), .Z(alu_multiplexerx2_1_z));
  ALU_MultiplexerX2 alu_multiplexerx2_2 (
    .S3(S2), .D0(alu_logic_1_z1), .D1(alu_arithmetic_1_z1), .Z(alu_multiplexerx2_2_z));
  ALU_MultiplexerX2 alu_multiplexerx2_3 (
    .S3(S2), .D0(alu_logic_1_z2), .D1(alu_arithmetic_1_z2), .Z(alu_multiplexerx2_3_z));
  ALU_MultiplexerX2 alu_multiplexerx2_4 (
    .S3(S2), .D0(alu_logic_1_z3), .D1(alu_arithmetic_1_z3), .Z(alu_multiplexerx2_4_z));
  ALU_MultiplexerX2 alu_multiplexerx2_5 (
    .S3(S2), .D0(alu_logic_1_z4), .D1(alu_arithmetic_1_z4), .Z(alu_multiplexerx2_5_z));
  ALU_MultiplexerX2 alu_multiplexerx2_6 (
    .S3(S2), .D0(alu_logic_1_z5), .D1(alu_arithmetic_1_z5), .Z(alu_multiplexerx2_6_z));
  ALU_MultiplexerX2 alu_multiplexerx2_7 (
    .S3(S2), .D0(alu_logic_1_z6), .D1(alu_arithmetic_1_z6), .Z(alu_multiplexerx2_7_z));
  ALU_MultiplexerX2 alu_multiplexerx2_8 (
    .S3(S2), .D0(alu_logic_1_z7), .D1(alu_arithmetic_1_z7), .Z(alu_multiplexerx2_8_z));
  ALU_Register alu_register_1 (
    .CLOCK(CLOCK), .D0(alu_multiplexerx2_1_z), .D1(alu_multiplexerx2_2_z), .D2(alu_multiplexerx2_3_z),
    .D3(alu_multiplexerx2_4_z), .D4(alu_multiplexerx2_5_z), .D5(alu_multiplexerx2_6_z),
    .D6(alu_multiplexerx2_7_z), .D7(alu_multiplexerx2_8_z), .Z0(Z0), .Z1(Z1), .Z2(Z2), .Z3(Z3), .Z4(Z4),
    .Z5(Z5), .Z6(Z6), .Z7(Z7));

  // Notes on the sheet:
  //   ADD = 0
  //   SUB =1 
  //   NOT = 000
  //   AND = 010
  //   OR = 100
  //   XOR = 110
  //   ADD/SUB = 001
  //   MULTI = 011
  //   DIV = 101
endmodule

module ALU_MultiplexerX4 (
  input  S0,
  input  S1,
  input  D0,
  input  D1,
  input  D2,
  input  D3,
  output Z
);

  wire and_1_out, and_2_out, and_3_out, and_4_out, not_1_out, not_2_out, not_3_out, not_4_out;

  not not_1 (not_1_out, S0);
  not not_2 (not_2_out, S1);
  not not_3 (not_3_out, S0);
  not not_4 (not_4_out, S1);
  and and_1 (and_1_out, not_1_out, not_2_out, D0);
  and and_2 (and_2_out, not_3_out, S1, D1);
  and and_3 (and_3_out, S0, not_4_out, D2);
  and and_4 (and_4_out, S0, S1, D3);
  or or_1 (Z, and_1_out, and_2_out, and_3_out, and_4_out);
endmodule

module ARITHMETIC_AdderSubtractor (
  input  SUB,
  input  A0,
  input  A1,
  input  A2,
  input  A3,
  input  A4,
  input  A5,
  input  A6,
  input  A7,
  input  B0,
  input  B1,
  input  B2,
  input  B3,
  input  B4,
  input  B5,
  input  B6,
  input  B7,
  output Z0,
  output Z1,
  output Z2,
  output Z3,
  output Z4,
  output Z5,
  output Z6,
  output Z7,
  output COUT
);

  wire and_1_out, and_2_out, and_3_out, and_4_out, and_5_out, and_6_out, and_7_out, and_8_out, and_9_out,
       and_10_out, and_11_out, and_12_out, and_13_out, and_14_out, and_15_out, and_16_out, or_1_out,
       or_2_out, or_3_out, or_4_out, or_5_out, or_6_out, or_7_out, xor_1_out, xor_2_out, xor_3_out,
       xor_4_out, xor_5_out, xor_6_out, xor_7_out, xor_8_out, xor_9_out, xor_10_out, xor_11_out, xor_12_out,
       xor_13_out, xor_14_out, xor_15_out, xor_16_out;

  xor xor_1 (xor_1_out, B0, SUB);
  xor xor_2 (xor_2_out, B1, SUB);
  xor xor_3 (xor_3_out, B2, SUB);
  xor xor_4 (xor_4_out, B3, SUB);
  xor xor_5 (xor_5_out, B4, SUB);
  xor xor_6 (xor_6_out, B5, SUB);
  xor xor_7 (xor_7_out, B6, SUB);
  xor xor_8 (xor_8_out, B7, SUB);
  xor xor_9 (xor_9_out, A0, xor_1_out);
  and and_1 (and_1_out, xor_1_out, A0);
  xor xor_10 (xor_10_out, A1, xor_2_out);
  and and_2 (and_2_out, xor_2_out, A1);
  xor xor_11 (xor_11_out, A2, xor_3_out);
  and and_3 (and_3_out, xor_3_out, A2);
  xor xor_12 (xor_12_out, A3, xor_4_out);
  and and_4 (and_4_out, xor_4_out, A3);
  xor xor_13 (xor_13_out, A4, xor_5_out);
  and and_5 (and_5_out, xor_5_out, A4);
  xor xor_14 (xor_14_out, A5, xor_6_out);
  and and_6 (and_6_out, xor_6_out, A5);
  xor xor_15 (xor_15_out, A6, xor_7_out);
  and and_7 (and_7_out, xor_7_out, A6);
  xor xor_16 (xor_16_out, A7, xor_8_out);
  and and_8 (and_8_out, xor_8_out, A7);
  and and_9 (and_9_out, SUB, xor_9_out);
  or or_1 (or_1_out, and_1_out, and_9_out);
  and and_10 (and_10_out, or_1_out, xor_10_out);
  or or_2 (or_2_out, and_2_out, and_10_out);
  and and_11 (and_11_out, or_2_out, xor_11_out);
  or or_3 (or_3_out, and_3_out, and_11_out);
  and and_12 (and_12_out, or_3_out, xor_12_out);
  or or_4 (or_4_out, and_4_out, and_12_out);
  and and_13 (and_13_out, or_4_out, xor_13_out);
  or or_5 (or_5_out, and_5_out, and_13_out);
  and and_14 (and_14_out, or_5_out, xor_14_out);
  or or_6 (or_6_out, and_6_out, and_14_out);
  and and_15 (and_15_out, or_6_out, xor_15_out);
  or or_7 (or_7_out, and_7_out, and_15_out);
  and and_16 (and_16_out, or_7_out, xor_16_out);
  or or_8 (COUT, and_8_out, and_16_out);
  xor xor_17 (Z0, SUB, xor_9_out);
  xor xor_18 (Z1, or_1_out, xor_10_out);
  xor xor_19 (Z2, or_2_out, xor_11_out);
  xor xor_20 (Z3, or_3_out, xor_12_out);
  xor xor_21 (Z4, or_4_out, xor_13_out);
  xor xor_22 (Z5, or_5_out, xor_14_out);
  xor xor_23 (Z6, or_6_out, xor_15_out);
  xor xor_24 (Z7, or_7_out, xor_16_out);
endmodule

module LOGIC_Or (
  input  A0,
  input  B0,
  input  A1,
  input  B1,
  input  A2,
  input  B2,
  input  A3,
  input  B3,
  input  A4,
  input  B4,
  input  A5,
  input  B5,
  input  A6,
  input  B6,
  input  A7,
  input  B7,
  output Z0,
  output Z1,
  output Z2,
  output Z3,
  output Z4,
  output Z5,
  output Z6,
  output Z7
);

  or or_1 (Z0, A0, B0);
  or or_2 (Z1, A1, B1);
  or or_3 (Z2, A2, B2);
  or or_4 (Z3, A3, B3);
  or or_5 (Z4, A4, B4);
  or or_6 (Z5, A5, B5);
  or or_7 (Z6, A6, B6);
  or or_8 (Z7, A7, B7);
endmodule

module LOGIC_And (
  input  A0,
  input  B0,
  input  A1,
  input  B1,
  input  A2,
  input  B2,
  input  A3,
  input  B3,
  input  A4,
  input  B4,
  input  A5,
  input  B5,
  input  A6,
  input  B6,
  input  A7,
  input  B7,
  output Z0,
  output Z1,
  output Z2,
  output Z3,
  output Z4,
  output Z5,
  output Z6,
  output Z7
);

  and and_1 (Z0, A0, B0);
  and and_2 (Z1, A1, B1);
  and and_3 (Z2, A2, B2);
  and and_4 (Z3, A3, B3);
  and and_5 (Z4, A4, B4);
  and and_6 (Z5, A5, B5);
  and and_7 (Z6, A6, B6);
  and and_8 (Z7, A7, B7);
endmodule

module ALU_Register (
  input  CLOCK,
  input  D0,
  input  D1,
  input  D2,
  input  D3,
  input  D4,
  input  D5,
  input  D6,
  input  D7,
  output Z0,
  output Z1,
  output Z2,
  output Z3,
  output Z4,
  output Z5,
  output Z6,
  output Z7
);

  wire nand_1_out, nand_2_out, nand_3_out, nand_4_out, nand_5_out, nand_6_out, nand_7_out, nand_8_out,
       nand_9_out, nand_10_out, nand_11_out, nand_12_out, nand_13_out, nand_14_out, nand_15_out, nand_16_out,
       nand_25_out, nand_26_out, nand_27_out, nand_28_out, nand_29_out, nand_30_out, nand_31_out,
       nand_32_out, not_1_out, not_2_out, not_3_out, not_4_out, not_5_out, not_6_out, not_7_out, not_8_out;

  not not_1 (not_1_out, D0);
  not not_2 (not_2_out, D1);
  not not_3 (not_3_out, D2);
  not not_4 (not_4_out, D3);
  not not_5 (not_5_out, D4);
  not not_6 (not_6_out, D5);
  not not_7 (not_7_out, D6);
  not not_8 (not_8_out, D7);
  nand nand_1 (nand_1_out, D0, CLOCK);
  nand nand_2 (nand_2_out, not_1_out, CLOCK);
  nand nand_3 (nand_3_out, D1, CLOCK);
  nand nand_4 (nand_4_out, not_2_out, CLOCK);
  nand nand_5 (nand_5_out, D2, CLOCK);
  nand nand_6 (nand_6_out, not_3_out, CLOCK);
  nand nand_7 (nand_7_out, D3, CLOCK);
  nand nand_8 (nand_8_out, not_4_out, CLOCK);
  nand nand_9 (nand_9_out, D4, CLOCK);
  nand nand_10 (nand_10_out, not_5_out, CLOCK);
  nand nand_11 (nand_11_out, D5, CLOCK);
  nand nand_12 (nand_12_out, not_6_out, CLOCK);
  nand nand_13 (nand_13_out, D6, CLOCK);
  nand nand_14 (nand_14_out, not_7_out, CLOCK);
  nand nand_15 (nand_15_out, D7, CLOCK);
  nand nand_16 (nand_16_out, not_8_out, CLOCK);
  nand nand_17 (Z0, nand_1_out, nand_25_out);
  nand nand_18 (Z1, nand_3_out, nand_26_out);
  nand nand_19 (Z2, nand_5_out, nand_27_out);
  nand nand_20 (Z3, nand_7_out, nand_28_out);
  nand nand_21 (Z4, nand_9_out, nand_29_out);
  nand nand_22 (Z5, nand_11_out, nand_30_out);
  nand nand_23 (Z6, nand_13_out, nand_31_out);
  nand nand_24 (Z7, nand_15_out, nand_32_out);
  nand nand_25 (nand_25_out, Z0, nand_2_out);
  nand nand_26 (nand_26_out, Z1, nand_4_out);
  nand nand_27 (nand_27_out, Z2, nand_6_out);
  nand nand_28 (nand_28_out, Z3, nand_8_out);
  nand nand_29 (nand_29_out, Z4, nand_10_out);
  nand nand_30 (nand_30_out, Z5, nand_12_out);
  nand nand_31 (nand_31_out, Z6, nand_14_out);
  nand nand_32 (nand_32_out, Z7, nand_16_out);
endmodule

module LOGIC_Xor (
  input  A0,
  input  B0,
  input  A1,
  input  B1,
  input  A2,
  input  B2,
  input  A3,
  input  B3,
  input  A4,
  input  B4,
  input  A5,
  input  B5,
  input  A6,
  input  B6,
  input  A7,
  input  B7,
  output Z0,
  output Z1,
  output Z2,
  output Z3,
  output Z4,
  output Z5,
  output Z6,
  output Z7
);

  xor xor_1 (Z0, A0, B0);
  xor xor_2 (Z1, A1, B1);
  xor xor_3 (Z2, A2, B2);
  xor xor_4 (Z3, A3, B3);
  xor xor_5 (Z4, A4, B4);
  xor xor_6 (Z5, A5, B5);
  xor xor_7 (Z6, A6, B6);
  xor xor_8 (Z7, A7, B7);
endmodule

module ALU_Logic (
  input  A0,
  input  A1,
  input  A2,
  input  A3,
  input  A4,
  input  A5,
  input  A6,
  input  A7,
  input  B0,
  input  B1,
  input  B2,
  input  B3,
  input  B4,
  input  B5,
  input  B6,
  input  B7,
  input  S0,
  input  S1,
  output Z0,
  output Z1,
  output Z2,
  output Z3,
  output Z4,
  output Z5,
  output Z6,
  output Z7
);

  wire logic_and_1_z0, logic_and_1_z1, logic_and_1_z2, logic_and_1_z3, logic_and_1_z4, logic_and_1_z5,
       logic_and_1_z6, logic_and_1_z7, logic_or_1_z0, logic_or_1_z1, logic_or_1_z2, logic_or_1_z3,
       logic_or_1_z4, logic_or_1_z5, logic_or_1_z6, logic_or_1_z7, logic_xor_1_z0, logic_xor_1_z1,
       logic_xor_1_z2, logic_xor_1_z3, logic_xor_1_z4, logic_xor_1_z5, logic_xor_1_z6, logic_xor_1_z7,
       not_1_out, not_2_out, not_3_out, not_4_out, not_5_out, not_6_out, not_7_out, not_8_out;

  not not_1 (not_1_out, A0);
  not not_2 (not_2_out, A1);
  not not_3 (not_3_out, A2);
  not not_4 (not_4_out, A3);
  not not_5 (not_5_out, A4);
  not not_6 (not_6_out, A5);
  not not_7 (not_7_out, A6);
  not not_8 (not_8_out, A7);
  LOGIC_And logic_and_1 (
    .A0(A0), .B0(B0), .A1(A1), .B1(B1), .A2(A2), .B2(B2), .A3(A3), .B3(B3), .A4(A4), .B4(B4), .A5(A5),
    .B5(B5), .A6(A6), .B6(B6), .A7(A7), .B7(B7), .Z0(logic_and_1_z0), .Z1(logic_and_1_z1),
    .Z2(logic_and_1_z2), .Z3(logic_and_1_z3), .Z4(logic_and_1_z4), .Z5(logic_and_1_z5), .Z6(logic_and_1_z6),
    .Z7(logic_and_1_z7));
  LOGIC_Or logic_or_1 (
    .A0(A0), .B0(B0), .A1(A1), .B1(B1), .A2(A2), .B2(B2), .A3(A3), .B3(B3), .A4(A4), .B4(B4), .A5(A5),
    .B5(B5), .A6(A6), .B6(B6), .A7(A7), .B7(B7), .Z0(logic_or_1_z0), .Z1(logic_or_1_z1), .Z2(logic_or_1_z2),
    .Z3(logic_or_1_z3), .Z4(logic_or_1_z4), .Z5(logic_or_1_z5), .Z6(logic_or_1_z6), .Z7(logic_or_1_z7));
  LOGIC_Xor logic_xor_1 (
    .A0(A0), .B0(B0), .A1(A1), .B1(B1), .A2(A2), .B2(B2), .A3(A3), .B3(B3), .A4(A4), .B4(B4), .A5(A5),
    .B5(B5), .A6(A6), .B6(B6), .A7(A7), .B7(B7), .Z0(logic_xor_1_z0), .Z1(logic_xor_1_z1),
    .Z2(logic_xor_1_z2), .Z3(logic_xor_1_z3), .Z4(logic_xor_1_z4), .Z5(logic_xor_1_z5), .Z6(logic_xor_1_z6),
    .Z7(logic_xor_1_z7));
  ALU_MultiplexerX4 alu_multiplexerx4_1 (
    .S0(S0), .S1(S1), .D0(not_1_out), .D1(logic_and_1_z0), .D2(logic_or_1_z0), .D3(logic_xor_1_z0), .Z(Z0));
  ALU_MultiplexerX4 alu_multiplexerx4_2 (
    .S0(S0), .S1(S1), .D0(not_2_out), .D1(logic_and_1_z1), .D2(logic_or_1_z1), .D3(logic_xor_1_z1), .Z(Z1));
  ALU_MultiplexerX4 alu_multiplexerx4_3 (
    .S0(S0), .S1(S1), .D0(not_3_out), .D1(logic_and_1_z2), .D2(logic_or_1_z2), .D3(logic_xor_1_z2), .Z(Z2));
  ALU_MultiplexerX4 alu_multiplexerx4_4 (
    .S0(S0), .S1(S1), .D0(not_4_out), .D1(logic_and_1_z3), .D2(logic_or_1_z3), .D3(logic_xor_1_z3), .Z(Z3));
  ALU_MultiplexerX4 alu_multiplexerx4_5 (
    .S0(S0), .S1(S1), .D0(not_5_out), .D1(logic_and_1_z4), .D2(logic_or_1_z4), .D3(logic_xor_1_z4), .Z(Z4));
  ALU_MultiplexerX4 alu_multiplexerx4_6 (
    .S0(S0), .S1(S1), .D0(not_6_out), .D1(logic_and_1_z5), .D2(logic_or_1_z5), .D3(logic_xor_1_z5), .Z(Z5));
  ALU_MultiplexerX4 alu_multiplexerx4_7 (
    .S0(S0), .S1(S1), .D0(not_7_out), .D1(logic_and_1_z6), .D2(logic_or_1_z6), .D3(logic_xor_1_z6), .Z(Z6));
  ALU_MultiplexerX4 alu_multiplexerx4_8 (
    .S0(S0), .S1(S1), .D0(not_8_out), .D1(logic_and_1_z7), .D2(logic_or_1_z7), .D3(logic_xor_1_z7), .Z(Z7));
endmodule

module ALU_Arithmetic (
  input  A0,
  input  A1,
  input  A2,
  input  A3,
  input  A4,
  input  A5,
  input  A6,
  input  A7,
  input  B0,
  input  B1,
  input  B2,
  input  B3,
  input  B4,
  input  B5,
  input  B6,
  input  B7,
  input  SUB,
  input  S0,
  input  S1,
  output Z0,
  output Z1,
  output Z2,
  output Z3,
  output Z4,
  output Z5,
  output Z6,
  output Z7,
  output COUT
);

  wire arithmetic_addersubtractor_1_cout, arithmetic_addersubtractor_1_z0, arithmetic_addersubtractor_1_z1,
       arithmetic_addersubtractor_1_z2, arithmetic_addersubtractor_1_z3, arithmetic_addersubtractor_1_z4,
       arithmetic_addersubtractor_1_z5, arithmetic_addersubtractor_1_z6, arithmetic_addersubtractor_1_z7,
       arithmetic_divider_1_cout, arithmetic_divider_1_z0, arithmetic_divider_1_z1, arithmetic_divider_1_z2,
       arithmetic_divider_1_z3, arithmetic_divider_1_z4, arithmetic_divider_1_z5, arithmetic_divider_1_z6,
       arithmetic_divider_1_z7, arithmetic_multiplier_1_cout, arithmetic_multiplier_1_z0,
       arithmetic_multiplier_1_z1, arithmetic_multiplier_1_z2, arithmetic_multiplier_1_z3,
       arithmetic_multiplier_1_z4, arithmetic_multiplier_1_z5, arithmetic_multiplier_1_z6,
       arithmetic_multiplier_1_z7;

  ARITHMETIC_AdderSubtractor arithmetic_addersubtractor_1 (
    .SUB(SUB), .A0(A0), .A1(A1), .A2(A2), .A3(A3), .A4(A4), .A5(A5), .A6(A6), .A7(A7), .B0(B0), .B1(B1),
    .B2(B2), .B3(B3), .B4(B4), .B5(B5), .B6(B6), .B7(B7), .Z0(arithmetic_addersubtractor_1_z0),
    .Z1(arithmetic_addersubtractor_1_z1), .Z2(arithmetic_addersubtractor_1_z2),
    .Z3(arithmetic_addersubtractor_1_z3), .Z4(arithmetic_addersubtractor_1_z4),
    .Z5(arithmetic_addersubtractor_1_z5), .Z6(arithmetic_addersubtractor_1_z6),
    .Z7(arithmetic_addersubtractor_1_z7), .COUT(arithmetic_addersubtractor_1_cout));
  ARITHMETIC_Multiplier arithmetic_multiplier_1 (
    .A0(A0), .A1(A1), .A2(A2), .A3(A3), .A4(A4), .A5(A5), .A6(A6), .A7(A7), .B0(B0), .B1(B1), .B2(B2),
    .B3(B3), .B4(B4), .B5(B5), .B6(B6), .B7(B7), .Z0(arithmetic_multiplier_1_z0),
    .Z1(arithmetic_multiplier_1_z1), .Z2(arithmetic_multiplier_1_z2), .Z3(arithmetic_multiplier_1_z3),
    .Z4(arithmetic_multiplier_1_z4), .Z5(arithmetic_multiplier_1_z5), .Z6(arithmetic_multiplier_1_z6),
    .Z7(arithmetic_multiplier_1_z7), .COUT(arithmetic_multiplier_1_cout));
  ARITHMETIC_Divider arithmetic_divider_1 (
    .A0(A0), .A1(A1), .A2(A2), .A3(A3), .A4(A4), .A5(A5), .A6(A6), .A7(A7), .B0(B0), .B1(B1), .B2(B2),
    .B3(B3), .B4(B4), .B5(B5), .B6(B6), .B7(B7), .Z0(arithmetic_divider_1_z0), .Z1(arithmetic_divider_1_z1),
    .Z2(arithmetic_divider_1_z2), .Z3(arithmetic_divider_1_z3), .Z4(arithmetic_divider_1_z4),
    .Z5(arithmetic_divider_1_z5), .Z6(arithmetic_divider_1_z6), .Z7(arithmetic_divider_1_z7),
    .COUT(arithmetic_divider_1_cout));
  ALU_MultiplexerX4 alu_multiplexerx4_1 (
    .S0(S0), .S1(S1), .D0(arithmetic_addersubtractor_1_z0), .D1(arithmetic_multiplier_1_z0),
    .D2(arithmetic_divider_1_z0), .Z(Z0));  // open: D3
  ALU_MultiplexerX4 alu_multiplexerx4_2 (
    .S0(S0), .S1(S1), .D0(arithmetic_addersubtractor_1_z1), .D1(arithmetic_multiplier_1_z1),
    .D2(arithmetic_divider_1_z1), .Z(Z1));  // open: D3
  ALU_MultiplexerX4 alu_multiplexerx4_3 (
    .S0(S0), .S1(S1), .D0(arithmetic_addersubtractor_1_z2), .D1(arithmetic_multiplier_1_z2),
    .D2(arithmetic_divider_1_z2), .Z(Z2));  // open: D3
  ALU_MultiplexerX4 alu_multiplexerx4_4 (
    .S0(S0), .S1(S1), .D0(arithmetic_addersubtractor_1_z3), .D1(arithmetic_multiplier_1_z3),
    .D2(arithmetic_divider_1_z3), .Z(Z3));  // open: D3
  ALU_MultiplexerX4 alu_multiplexerx4_5 (
    .S0(S0), .S1(S1), .D0(arithmetic_addersubtractor_1_z4), .D1(arithmetic_multiplier_1_z4),
    .D2(arithmetic_divider_1_z4), .Z(Z4));  // open: D3
  ALU_MultiplexerX4 alu_multiplexerx4_6 (
    .S0(S0), .S1(S1), .D0(arithmetic_addersubtractor_1_z5), .D1(arithmetic_multiplier_1_z5),
    .D2(arithmetic_divider_1_z5), .Z(Z5));  // open: D3
  ALU_MultiplexerX4 alu_multiplexerx4_7 (
    .S0(S0), .S1(S1), .D0(arithmetic_addersubtractor_1_z6), .D1(arithmetic_multiplier_1_z6),
    .D2(arithmetic_divider_1_z6), .Z(Z6));  // open: D3
  ALU_MultiplexerX4 alu_multiplexerx4_8 (
    .S0(S0), .S1(S1), .D0(arithmetic_addersubtractor_1_z7), .D1(arithmetic_multiplier_1_z7),
    .D2(arithmetic_divider_1_z7), .Z(Z7));  // open: D3
  ALU_MultiplexerX4 alu_multiplexerx4_9 (
    .S0(S0), .S1(S1), .D0(arithmetic_addersubtractor_1_cout), .D1(arithmetic_multiplier_1_cout),
    .D2(arithmetic_divider_1_cout), .Z(COUT));  // open: D3
endmodule

module ARITHMETIC_Multiplier (
  input  A0,
  input  A1,
  input  A2,
  input  A3,
  input  A4,
  input  A5,
  input  A6,
  input  A7,
  input  B0,
  input  B1,
  input  B2,
  input  B3,
  input  B4,
  input  B5,
  input  B6,
  input  B7,
  output Z0,
  output Z1,
  output Z2,
  output Z3,
  output Z4,
  output Z5,
  output Z6,
  output Z7,
  output COUT
);
endmodule

module ALU_MultiplexerX2 (
  input  S3,
  input  D0,
  input  D1,
  output Z
);

  wire and_1_out, and_2_out, not_1_out;

  not not_1 (not_1_out, S3);
  and and_1 (and_1_out, not_1_out, D0);
  and and_2 (and_2_out, S3, D1);
  or or_1 (Z, and_1_out, and_2_out);
endmodule

module ARITHMETIC_Divider (
  input  A0,
  input  A1,
  input  A2,
  input  A3,
  input  A4,
  input  A5,
  input  A6,
  input  A7,
  input  B0,
  input  B1,
  input  B2,
  input  B3,
  input  B4,
  input  B5,
  input  B6,
  input  B7,
  output Z0,
  output Z1,
  output Z2,
  output Z3,
  output Z4,
  output Z5,
  output Z6,
  output Z7,
  output COUT
);
endmodule
